// Logisim project projeto_ula_completa.circ as structural Verilog: 12 circuits, main circuit main
module main (
  input  [4:0] in_1,
  input  in_2,
  input  [31:0] in_3,
  input  in_4,
  output [31:0] out_5
);

  wire clock_1_out, processador_1_out_8, processador_1_out_9;
  wire [7:0] processador_1_seletor;
  wire [19:0] ram_1_data;

  Clock clock_1 (.out(clock_1_out));
  RAM #(.dataWidth(20)) ram_1 (.addr(processador_1_seletor), .data(ram_1_data));  // open: sel, clk, ld, clr
  processador processador_1 (
    .in_2(in_3), .in_4(in_1), .out_7(out_5), .out_8(processador_1_out_8), .I(in_2),
    .out_9(processador_1_out_9), .in_1(clock_1_out), .in_6(in_4), .Seletor(processador_1_seletor),
    .in_5(ram_1_data));
  LED led_1 (.in(processador_1_out_8));
  LED led_2 (.in(processador_1_out_9));

  // Notes on the sheet:
  //   00000 - AND
  //   00001 - OR
  //   00010 - NAND
  //   00011 - XOR  
  //    00100 - SOM N
  //    00101 - SOM Z
  //   00110 - SUB N
  //   00111 - SLT
  //   01000 - SLL
  //   01001 - SRL
  //   01010 - SRA
endmodule

module ula_cel (
  input  c_in,
  input  A,
  input  B,
  input  [4:0] in_4,
  input  LESS,
  output out_6,
  output out_7,
  output SET
);

  wire adder_1_cout, adder_1_out, adder_2_cout, adder_2_out, and_1_out, nand_1_out, or_1_out,
       subtractor_1_bout, xor_1_out;

  and and_1 (and_1_out, A, B);
  or or_1 (or_1_out, A, B);
  nand nand_1 (nand_1_out, A, B);
  xor xor_1 (xor_1_out, A, B);
  Adder #(.width(1)) adder_1 (.a(A), .b(B), .out(adder_1_out), .cin(c_in), .cout(adder_1_cout));
  Adder #(.width(1)) adder_2 (.a(A), .b(B), .out(adder_2_out), .cin(c_in), .cout(adder_2_cout));
  Subtractor #(.width(1)) subtractor_1 (.a(A), .b(B), .out(SET), .bin(c_in), .bout(subtractor_1_bout));
  Multiplexer #(.select(5), .enable("false")) multiplexer_1 (
    .in0(and_1_out), .in1(or_1_out), .in2(nand_1_out), .in3(xor_1_out), .in4(adder_1_out), .in5(adder_2_out),
    .in6(SET), .in7(LESS), .out(out_6), .sel(in_4));  // open: in8, in9, in10, in11, in12, in13, in14, in15, in16, in17, in18, in19, in20, in21, in22, in23, in24, in25, in26, in27, in28, in29, in30, in31
  Multiplexer #(.select(5), .enable("false")) multiplexer_2 (
    .in4(adder_1_cout), .in5(adder_2_cout), .in6(subtractor_1_bout), .in7(subtractor_1_bout), .out(out_7),
    .sel(in_4));  // open: in0, in1, in2, in3, in8, in9, in10, in11, in12, in13, in14, in15, in16, in17, in18, in19, in20, in21, in22, in23, in24, in25, in26, in27, in28, in29, in30, in31

  // Notes on the sheet:
  //   N
  //   I
  //   N
endmodule

module overflow (
  input  [3:0] in_1,
  input  [4:0] in_2,
  output out_3
);

  wire and_1_out, and_2_out, and_3_out, and_4_out, or_1_out, or_2_out, undriven;

  and and_1 (and_1_out, in_1[1], in_1[2], ~in_1[3]);  // AND_Gate
  and and_2 (and_2_out, ~in_1[1], ~in_1[2], in_1[3]);  // AND_Gate
  and and_3 (and_3_out, ~in_1[1], in_1[2], in_1[3]);  // AND_Gate
  and and_4 (and_4_out, in_1[1], ~in_1[2], ~in_1[3]);  // AND_Gate
  or or_1 (or_1_out, and_1_out, and_2_out);
  or or_2 (or_2_out, and_3_out, and_4_out);
  Multiplexer #(.select(5), .enable("false")) multiplexer_1 (
    .in4(in_1[0]), .in5(or_1_out), .in6(in_1[0]), .in7(or_2_out), .in16(undriven), .in17(undriven),
    .out(out_3), .sel(in_2));  // open: in0, in1, in2, in3, in8, in9, in10, in11, in12, in13, in14, in15, in18, in19, in20, in21, in22, in23, in24, in25, in26, in27, in28, in29, in30, in31

  // Notes on the sheet:
  //   Overflow + Inteiros
  //   Overflow +/- Naturais
  //   Overflow -
  //   Seletor de operação
endmodule

module ula (
  input  [4:0] in_1,
  input  [31:0] in_2,
  input  [31:0] in_3,
  input  [4:0] in_4,
  output [31:0] out_5,
  output Saida_0,
  output out_7
);

  wire ula_cel_1_out_7, ula_cel_2_out_7, ula_cel_3_out_7, ula_cel_4_out_7, ula_cel_5_out_7, ula_cel_6_out_7,
       ula_cel_7_out_7, ula_cel_8_out_7, ula_cel_9_out_7, ula_cel_10_out_7, ula_cel_11_out_7,
       ula_cel_12_out_7, ula_cel_13_out_7, ula_cel_14_out_7, ula_cel_15_out_7, ula_cel_16_out_7,
       ula_cel_17_out_7, ula_cel_18_out_7, ula_cel_19_out_7, ula_cel_20_out_7, ula_cel_21_out_7,
       ula_cel_22_out_7, ula_cel_23_out_7, ula_cel_24_out_7, ula_cel_25_out_7, ula_cel_26_out_7,
       ula_cel_27_out_7, ula_cel_28_out_7, ula_cel_29_out_7, ula_cel_30_out_7, ula_cel_31_out_7,
       ula_cel_32_set;
  wire [3:0] ula_cel_32_out_7;
  wire [31:0] sll_1_out_3, sra_1_out_3, srl_1_out_3, ula_cel_1_out_6;

  nor nor_1 (Saida_0, out_5[31], out_5[30], out_5[29], out_5[28], out_5[27], out_5[26], out_5[25], out_5[24], out_5[23], out_5[22], out_5[21], out_5[20], out_5[19], out_5[18], out_5[17], out_5[16], out_5[15], out_5[14], out_5[13], out_5[12], out_5[11], out_5[10], out_5[9], out_5[8], out_5[7], out_5[6], out_5[5], out_5[4], out_5[3], out_5[2], out_5[1], out_5[0]);
  ula_cel ula_cel_1 (
    .c_in(1'b0), .out_6(ula_cel_1_out_6[0]), .A(in_2[0]), .B(in_3[0]), .in_4(in_4), .LESS(ula_cel_32_set),
    .out_7(ula_cel_1_out_7));  // open: SET
  ula_cel ula_cel_2 (
    .c_in(ula_cel_31_out_7), .out_6(ula_cel_1_out_6[16]), .A(in_2[16]), .B(in_3[16]), .in_4(in_4),
    .LESS(1'b0), .out_7(ula_cel_2_out_7));  // open: SET
  ula_cel ula_cel_3 (
    .c_in(ula_cel_1_out_7), .out_6(ula_cel_1_out_6[1]), .A(in_2[1]), .B(in_3[1]), .in_4(in_4), .LESS(1'b0),
    .out_7(ula_cel_3_out_7));  // open: SET
  ula_cel ula_cel_4 (
    .c_in(ula_cel_2_out_7), .out_6(ula_cel_1_out_6[17]), .A(in_2[17]), .B(in_3[17]), .in_4(in_4),
    .LESS(1'b0), .out_7(ula_cel_4_out_7));  // open: SET
  ula_cel ula_cel_5 (
    .c_in(ula_cel_3_out_7), .out_6(ula_cel_1_out_6[2]), .A(in_2[2]), .B(in_3[2]), .in_4(in_4), .LESS(1'b0),
    .out_7(ula_cel_5_out_7));  // open: SET
  ula_cel ula_cel_6 (
    .c_in(ula_cel_4_out_7), .out_6(ula_cel_1_out_6[18]), .A(in_2[18]), .B(in_3[18]), .in_4(in_4),
    .LESS(1'b0), .out_7(ula_cel_6_out_7));  // open: SET
  ula_cel ula_cel_7 (
    .c_in(ula_cel_5_out_7), .out_6(ula_cel_1_out_6[3]), .A(in_2[3]), .B(in_3[3]), .in_4(in_4), .LESS(1'b0),
    .out_7(ula_cel_7_out_7));  // open: SET
  ula_cel ula_cel_8 (
    .c_in(ula_cel_6_out_7), .out_6(ula_cel_1_out_6[19]), .A(in_2[19]), .B(in_3[19]), .in_4(in_4),
    .LESS(1'b0), .out_7(ula_cel_8_out_7));  // open: SET
  ula_cel ula_cel_9 (
    .c_in(ula_cel_7_out_7), .out_6(ula_cel_1_out_6[4]), .A(in_2[4]), .B(in_3[4]), .in_4(in_4), .LESS(1'b0),
    .out_7(ula_cel_9_out_7));  // open: SET
  ula_cel ula_cel_10 (
    .c_in(ula_cel_8_out_7), .out_6(ula_cel_1_out_6[20]), .A(in_2[20]), .B(in_3[20]), .in_4(in_4),
    .LESS(1'b0), .out_7(ula_cel_10_out_7));  // open: SET
  ula_cel ula_cel_11 (
    .c_in(ula_cel_9_out_7), .out_6(ula_cel_1_out_6[5]), .A(in_2[5]), .B(in_3[5]), .in_4(in_4), .LESS(1'b0),
    .out_7(ula_cel_11_out_7));  // open: SET
  ula_cel ula_cel_12 (
    .c_in(ula_cel_10_out_7), .out_6(ula_cel_1_out_6[21]), .A(in_2[21]), .B(in_3[21]), .in_4(in_4),
    .LESS(1'b0), .out_7(ula_cel_12_out_7));  // open: SET
  ula_cel ula_cel_13 (
    .c_in(ula_cel_11_out_7), .out_6(ula_cel_1_out_6[6]), .A(in_2[6]), .B(in_3[6]), .in_4(in_4), .LESS(1'b0),
    .out_7(ula_cel_13_out_7));  // open: SET
  ula_cel ula_cel_14 (
    .c_in(ula_cel_12_out_7), .out_6(ula_cel_1_out_6[22]), .A(in_2[22]), .B(in_3[22]), .in_4(in_4),
    .LESS(1'b0), .out_7(ula_cel_14_out_7));  // open: SET
  ula_cel ula_cel_15 (
    .c_in(ula_cel_13_out_7), .out_6(ula_cel_1_out_6[7]), .A(in_2[7]), .B(in_3[7]), .in_4(in_4), .LESS(1'b0),
    .out_7(ula_cel_15_out_7));  // open: SET
  ula_cel ula_cel_16 (
    .c_in(ula_cel_14_out_7), .out_6(ula_cel_1_out_6[23]), .A(in_2[23]), .B(in_3[23]), .in_4(in_4),
    .LESS(1'b0), .out_7(ula_cel_16_out_7));  // open: SET
  ula_cel ula_cel_17 (
    .c_in(ula_cel_15_out_7), .out_6(ula_cel_1_out_6[8]), .A(in_2[8]), .B(in_3[8]), .in_4(in_4), .LESS(1'b0),
    .out_7(ula_cel_17_out_7));  // open: SET
  ula_cel ula_cel_18 (
    .c_in(ula_cel_16_out_7), .out_6(ula_cel_1_out_6[24]), .A(in_2[24]), .B(in_3[24]), .in_4(in_4),
    .LESS(1'b0), .out_7(ula_cel_18_out_7));  // open: SET
  ula_cel ula_cel_19 (
    .c_in(ula_cel_17_out_7), .out_6(ula_cel_1_out_6[9]), .A(in_2[9]), .B(in_3[9]), .in_4(in_4), .LESS(1'b0),
    .out_7(ula_cel_19_out_7));  // open: SET
  ula_cel ula_cel_20 (
    .c_in(ula_cel_18_out_7), .out_6(ula_cel_1_out_6[25]), .A(in_2[25]), .B(in_3[25]), .in_4(in_4),
    .LESS(1'b0), .out_7(ula_cel_20_out_7));  // open: SET
  ula_cel ula_cel_21 (
    .c_in(ula_cel_19_out_7), .out_6(ula_cel_1_out_6[10]), .A(in_2[10]), .B(in_3[10]), .in_4(in_4),
    .LESS(1'b0), .out_7(ula_cel_21_out_7));  // open: SET
  ula_cel ula_cel_22 (
    .c_in(ula_cel_20_out_7), .out_6(ula_cel_1_out_6[26]), .A(in_2[26]), .B(in_3[26]), .in_4(in_4),
    .LESS(1'b0), .out_7(ula_cel_22_out_7));  // open: SET
  ula_cel ula_cel_23 (
    .c_in(ula_cel_21_out_7), .out_6(ula_cel_1_out_6[11]), .A(in_2[11]), .B(in_3[11]), .in_4(in_4),
    .LESS(1'b0), .out_7(ula_cel_23_out_7));  // open: SET
  ula_cel ula_cel_24 (
    .c_in(ula_cel_22_out_7), .out_6(ula_cel_1_out_6[27]), .A(in_2[27]), .B(in_3[27]), .in_4(in_4),
    .LESS(1'b0), .out_7(ula_cel_24_out_7));  // open: SET
  ula_cel ula_cel_25 (
    .c_in(ula_cel_23_out_7), .out_6(ula_cel_1_out_6[12]), .A(in_2[12]), .B(in_3[12]), .in_4(in_4),
    .LESS(1'b0), .out_7(ula_cel_25_out_7));  // open: SET
  ula_cel ula_cel_26 (
    .c_in(ula_cel_24_out_7), .out_6(ula_cel_1_out_6[28]), .A(in_2[28]), .B(in_3[28]), .in_4(in_4),
    .LESS(1'b0), .out_7(ula_cel_26_out_7));  // open: SET
  ula_cel ula_cel_27 (
    .c_in(ula_cel_25_out_7), .out_6(ula_cel_1_out_6[13]), .A(in_2[13]), .B(in_3[13]), .in_4(in_4),
    .LESS(1'b0), .out_7(ula_cel_27_out_7));  // open: SET
  ula_cel ula_cel_28 (
    .c_in(ula_cel_26_out_7), .out_6(ula_cel_1_out_6[29]), .A(in_2[29]), .B(in_3[29]), .in_4(in_4),
    .LESS(1'b0), .out_7(ula_cel_28_out_7));  // open: SET
  ula_cel ula_cel_29 (
    .c_in(ula_cel_27_out_7), .out_6(ula_cel_1_out_6[14]), .A(in_2[14]), .B(in_3[14]), .in_4(in_4),
    .LESS(1'b0), .out_7(ula_cel_29_out_7));  // open: SET
  ula_cel ula_cel_30 (
    .c_in(ula_cel_28_out_7), .out_6(ula_cel_1_out_6[30]), .A(in_2[30]), .B(in_3[30]), .in_4(in_4),
    .LESS(1'b0), .out_7(ula_cel_30_out_7));  // open: SET
  Multiplexer #(.select(5), .width(32), .enable("false")) multiplexer_1 (
    .in0(ula_cel_1_out_6), .in1(ula_cel_1_out_6), .in2(ula_cel_1_out_6), .in3(ula_cel_1_out_6),
    .in4(ula_cel_1_out_6), .in5(ula_cel_1_out_6), .in6(ula_cel_1_out_6), .in7(ula_cel_1_out_6),
    .in8(sll_1_out_3), .in9(srl_1_out_3), .in10(sra_1_out_3), .out(out_5), .sel(in_4));  // open: in11, in12, in13, in14, in15, in16, in17, in18, in19, in20, in21, in22, in23, in24, in25, in26, in27, in28, in29, in30, in31
  ula_cel ula_cel_31 (
    .c_in(ula_cel_29_out_7), .out_6(ula_cel_1_out_6[15]), .A(in_2[15]), .B(in_3[15]), .in_4(in_4),
    .LESS(1'b0), .out_7(ula_cel_31_out_7));  // open: SET
  ula_cel ula_cel_32 (
    .c_in(ula_cel_30_out_7), .out_6(ula_cel_1_out_6[31]), .A(in_2[31]), .B(in_3[31]), .in_4(in_4),
    .SET(ula_cel_32_set), .LESS(1'b0), .out_7(ula_cel_32_out_7[0]));
  or or_1 (ula_cel_32_out_7[3], ula_cel_32_set, ula_cel_1_out_6[31]);
  overflow overflow_1 (
    .in_2(in_4), .out_3(out_7), .in_1({ula_cel_32_out_7[3], in_3[31], in_2[31], ula_cel_32_out_7[0]}));
  SLL sll_1 (.out_3(sll_1_out_3), .in_1(in_1), .in_2(in_2));
  SRL srl_1 (.out_3(srl_1_out_3), .in_1(in_1), .in_2(in_2));
  SRA sra_1 (.out_3(sra_1_out_3), .in_1(in_1), .in_2(in_2));

  // Notes on the sheet:
  //   Oper
  //   Entrada A
  //   +/-
  //   Entrada B
  //   Saida S
endmodule

module SLL (
  input  [4:0] in_1,
  input  [31:0] in_2,
  output [31:0] out_3
);

  wire multiplexer_1_out, multiplexer_2_out, multiplexer_3_out, multiplexer_4_out, multiplexer_5_out,
       multiplexer_6_out, multiplexer_7_out, multiplexer_8_out, multiplexer_9_out, multiplexer_10_out,
       multiplexer_11_out, multiplexer_12_out, multiplexer_13_out, multiplexer_14_out, multiplexer_15_out,
       multiplexer_16_out, multiplexer_17_out, multiplexer_18_out, multiplexer_19_out, multiplexer_20_out,
       multiplexer_21_out, multiplexer_22_out, multiplexer_23_out, multiplexer_24_out, multiplexer_25_out,
       multiplexer_26_out, multiplexer_27_out, multiplexer_28_out, multiplexer_29_out, multiplexer_30_out,
       multiplexer_31_out, multiplexer_32_out, multiplexer_33_out, multiplexer_34_out, multiplexer_35_out,
       multiplexer_36_out, multiplexer_37_out, multiplexer_38_out, multiplexer_39_out, multiplexer_40_out,
       multiplexer_41_out, multiplexer_42_out, multiplexer_43_out, multiplexer_44_out, multiplexer_45_out,
       multiplexer_46_out, multiplexer_47_out, multiplexer_48_out, multiplexer_49_out, multiplexer_50_out,
       multiplexer_51_out, multiplexer_52_out, multiplexer_53_out, multiplexer_54_out, multiplexer_55_out,
       multiplexer_56_out, multiplexer_57_out, multiplexer_58_out, multiplexer_59_out, multiplexer_60_out,
       multiplexer_61_out, multiplexer_62_out, multiplexer_63_out, multiplexer_64_out, multiplexer_65_out,
       multiplexer_66_out, multiplexer_67_out, multiplexer_68_out, multiplexer_69_out, multiplexer_70_out,
       multiplexer_71_out, multiplexer_72_out, multiplexer_73_out, multiplexer_74_out, multiplexer_75_out,
       multiplexer_76_out, multiplexer_77_out, multiplexer_78_out, multiplexer_79_out, multiplexer_80_out,
       multiplexer_81_out, multiplexer_82_out, multiplexer_83_out, multiplexer_84_out, multiplexer_85_out,
       multiplexer_86_out, multiplexer_87_out, multiplexer_88_out, multiplexer_89_out, multiplexer_90_out,
       multiplexer_91_out, multiplexer_92_out, multiplexer_93_out, multiplexer_94_out, multiplexer_95_out,
       multiplexer_96_out, multiplexer_97_out, multiplexer_98_out, multiplexer_99_out, multiplexer_100_out,
       multiplexer_101_out, multiplexer_102_out, multiplexer_103_out, multiplexer_104_out,
       multiplexer_105_out, multiplexer_106_out, multiplexer_107_out, multiplexer_108_out,
       multiplexer_109_out, multiplexer_110_out, multiplexer_111_out, multiplexer_112_out,
       multiplexer_113_out, multiplexer_114_out, multiplexer_115_out, multiplexer_116_out,
       multiplexer_117_out, multiplexer_118_out, multiplexer_119_out, multiplexer_120_out,
       multiplexer_121_out, multiplexer_122_out, multiplexer_123_out, multiplexer_124_out,
       multiplexer_125_out, multiplexer_126_out, multiplexer_127_out, multiplexer_128_out;

  Multiplexer #(.enable("false")) multiplexer_1 (
    .in0(in_2[31]), .in1(in_2[30]), .out(multiplexer_1_out), .sel(in_1[0]));
  Multiplexer #(.enable("false")) multiplexer_2 (
    .in0(in_2[30]), .in1(in_2[29]), .out(multiplexer_2_out), .sel(in_1[0]));
  Multiplexer #(.enable("false")) multiplexer_3 (
    .in0(in_2[29]), .in1(in_2[28]), .out(multiplexer_3_out), .sel(in_1[0]));
  Multiplexer #(.enable("false")) multiplexer_4 (
    .in0(in_2[28]), .in1(in_2[27]), .out(multiplexer_4_out), .sel(in_1[0]));
  Multiplexer #(.enable("false")) multiplexer_5 (
    .in0(in_2[27]), .in1(in_2[26]), .out(multiplexer_5_out), .sel(in_1[0]));
  Multiplexer #(.enable("false")) multiplexer_6 (
    .in0(in_2[26]), .in1(in_2[25]), .out(multiplexer_6_out), .sel(in_1[0]));
  Multiplexer #(.enable("false")) multiplexer_7 (
    .in0(in_2[25]), .in1(in_2[24]), .out(multiplexer_7_out), .sel(in_1[0]));
  Multiplexer #(.enable("false")) multiplexer_8 (
    .in0(in_2[24]), .in1(in_2[23]), .out(multiplexer_8_out), .sel(in_1[0]));
  Multiplexer #(.enable("false")) multiplexer_9 (
    .in0(in_2[23]), .in1(in_2[22]), .out(multiplexer_9_out), .sel(in_1[0]));
  Multiplexer #(.enable("false")) multiplexer_10 (
    .in0(in_2[22]), .in1(in_2[21]), .out(multiplexer_10_out), .sel(in_1[0]));
  Multiplexer #(.enable("false")) multiplexer_11 (
    .in0(in_2[21]), .in1(in_2[20]), .out(multiplexer_11_out), .sel(in_1[0]));
  Multiplexer #(.enable("false")) multiplexer_12 (
    .in0(in_2[20]), .in1(in_2[19]), .out(multiplexer_12_out), .sel(in_1[0]));
  Multiplexer #(.enable("false")) multiplexer_13 (
    .in0(in_2[19]), .in1(in_2[18]), .out(multiplexer_13_out), .sel(in_1[0]));
  Multiplexer #(.enable("false")) multiplexer_14 (
    .in0(in_2[18]), .in1(in_2[17]), .out(multiplexer_14_out), .sel(in_1[0]));
  Multiplexer #(.enable("false")) multiplexer_15 (
    .in0(in_2[17]), .in1(in_2[16]), .out(multiplexer_15_out), .sel(in_1[0]));
  Multiplexer #(.enable("false")) multiplexer_16 (
    .in0(in_2[16]), .in1(in_2[15]), .out(multiplexer_16_out), .sel(in_1[0]));
  Multiplexer #(.enable("false")) multiplexer_17 (
    .in0(in_2[15]), .in1(in_2[14]), .out(multiplexer_17_out), .sel(in_1[0]));
  Multiplexer #(.enable("false")) multiplexer_18 (
    .in0(in_2[14]), .in1(in_2[13]), .out(multiplexer_18_out), .sel(in_1[0]));
  Multiplexer #(.enable("false")) multiplexer_19 (
    .in0(in_2[13]), .in1(in_2[12]), .out(multiplexer_19_out), .sel(in_1[0]));
  Multiplexer #(.enable("false")) multiplexer_20 (
    .in0(in_2[12]), .in1(in_2[11]), .out(multiplexer_20_out), .sel(in_1[0]));
  Multiplexer #(.enable("false")) multiplexer_21 (
    .in0(in_2[11]), .in1(in_2[10]), .out(multiplexer_21_out), .sel(in_1[0]));
  Multiplexer #(.enable("false")) multiplexer_22 (
    .in0(in_2[10]), .in1(in_2[9]), .out(multiplexer_22_out), .sel(in_1[0]));
  Multiplexer #(.enable("false")) multiplexer_23 (
    .in0(in_2[9]), .in1(in_2[8]), .out(multiplexer_23_out), .sel(in_1[0]));
  Multiplexer #(.enable("false")) multiplexer_24 (
    .in0(in_2[8]), .in1(in_2[7]), .out(multiplexer_24_out), .sel(in_1[0]));
  Multiplexer #(.enable("false")) multiplexer_25 (
    .in0(in_2[7]), .in1(in_2[6]), .out(multiplexer_25_out), .sel(in_1[0]));
  Multiplexer #(.enable("false")) multiplexer_26 (
    .in0(in_2[6]), .in1(in_2[5]), .out(multiplexer_26_out), .sel(in_1[0]));
  Multiplexer #(.enable("false")) multiplexer_27 (
    .in0(in_2[5]), .in1(in_2[4]), .out(multiplexer_27_out), .sel(in_1[0]));
  Multiplexer #(.enable("false")) multiplexer_28 (
    .in0(in_2[4]), .in1(in_2[3]), .out(multiplexer_28_out), .sel(in_1[0]));
  Multiplexer #(.enable("false")) multiplexer_29 (
    .in0(in_2[3]), .in1(in_2[2]), .out(multiplexer_29_out), .sel(in_1[0]));
  Multiplexer #(.enable("false")) multiplexer_30 (
    .in0(in_2[2]), .in1(in_2[1]), .out(multiplexer_30_out), .sel(in_1[0]));
  Multiplexer #(.enable("false")) multiplexer_31 (
    .in0(in_2[1]), .in1(in_2[0]), .out(multiplexer_31_out), .sel(in_1[0]));
  Multiplexer #(.enable("false")) multiplexer_32 (.in0(in_2[0]), .in1(1'b0), .out(multiplexer_32_out), .sel(in_1[0]));
  Multiplexer #(.enable("false")) multiplexer_33 (
    .in0(multiplexer_1_out), .in1(multiplexer_3_out), .out(multiplexer_33_out), .sel(in_1[1]));
  Multiplexer #(.enable("false")) multiplexer_34 (
    .in0(multiplexer_2_out), .in1(multiplexer_4_out), .out(multiplexer_34_out), .sel(in_1[1]));
  Multiplexer #(.enable("false")) multiplexer_35 (
    .in0(multiplexer_3_out), .in1(multiplexer_5_out), .out(multiplexer_35_out), .sel(in_1[1]));
  Multiplexer #(.enable("false")) multiplexer_36 (
    .in0(multiplexer_4_out), .in1(multiplexer_6_out), .out(multiplexer_36_out), .sel(in_1[1]));
  Multiplexer #(.enable("false")) multiplexer_37 (
    .in0(multiplexer_5_out), .in1(multiplexer_7_out), .out(multiplexer_37_out), .sel(in_1[1]));
  Multiplexer #(.enable("false")) multiplexer_38 (
    .in0(multiplexer_6_out), .in1(multiplexer_8_out), .out(multiplexer_38_out), .sel(in_1[1]));
  Multiplexer #(.enable("false")) multiplexer_39 (
    .in0(multiplexer_7_out), .in1(multiplexer_9_out), .out(multiplexer_39_out), .sel(in_1[1]));
  Multiplexer #(.enable("false")) multiplexer_40 (
    .in0(multiplexer_8_out), .in1(multiplexer_10_out), .out(multiplexer_40_out), .sel(in_1[1]));
  Multiplexer #(.enable("false")) multiplexer_41 (
    .in0(multiplexer_9_out), .in1(multiplexer_11_out), .out(multiplexer_41_out), .sel(in_1[1]));
  Multiplexer #(.enable("false")) multiplexer_42 (
    .in0(multiplexer_10_out), .in1(multiplexer_12_out), .out(multiplexer_42_out), .sel(in_1[1]));
  Multiplexer #(.enable("false")) multiplexer_43 (
    .in0(multiplexer_11_out), .in1(multiplexer_13_out), .out(multiplexer_43_out), .sel(in_1[1]));
  Multiplexer #(.enable("false")) multiplexer_44 (
    .in0(multiplexer_12_out), .in1(multiplexer_14_out), .out(multiplexer_44_out), .sel(in_1[1]));
  Multiplexer #(.enable("false")) multiplexer_45 (
    .in0(multiplexer_13_out), .in1(multiplexer_15_out), .out(multiplexer_45_out), .sel(in_1[1]));
  Multiplexer #(.enable("false")) multiplexer_46 (
    .in0(multiplexer_14_out), .in1(multiplexer_16_out), .out(multiplexer_46_out), .sel(in_1[1]));
  Multiplexer #(.enable("false")) multiplexer_47 (
    .in0(multiplexer_15_out), .in1(multiplexer_17_out), .out(multiplexer_47_out), .sel(in_1[1]));
  Multiplexer #(.enable("false")) multiplexer_48 (
    .in0(multiplexer_16_out), .in1(multiplexer_18_out), .out(multiplexer_48_out), .sel(in_1[1]));
  Multiplexer #(.enable("false")) multiplexer_49 (
    .in0(multiplexer_17_out), .in1(multiplexer_19_out), .out(multiplexer_49_out), .sel(in_1[1]));
  Multiplexer #(.enable("false")) multiplexer_50 (
    .in0(multiplexer_18_out), .in1(multiplexer_20_out), .out(multiplexer_50_out), .sel(in_1[1]));
  Multiplexer #(.enable("false")) multiplexer_51 (
    .in0(multiplexer_19_out), .in1(multiplexer_21_out), .out(multiplexer_51_out), .sel(in_1[1]));
  Multiplexer #(.enable("false")) multiplexer_52 (
    .in0(multiplexer_20_out), .in1(multiplexer_22_out), .out(multiplexer_52_out), .sel(in_1[1]));
  Multiplexer #(.enable("false")) multiplexer_53 (
    .in0(multiplexer_21_out), .in1(multiplexer_23_out), .out(multiplexer_53_out), .sel(in_1[1]));
  Multiplexer #(.enable("false")) multiplexer_54 (
    .in0(multiplexer_22_out), .in1(multiplexer_24_out), .out(multiplexer_54_out), .sel(in_1[1]));
  Multiplexer #(.enable("false")) multiplexer_55 (
    .in0(multiplexer_23_out), .in1(multiplexer_25_out), .out(multiplexer_55_out), .sel(in_1[1]));
  Multiplexer #(.enable("false")) multiplexer_56 (
    .in0(multiplexer_24_out), .in1(multiplexer_26_out), .out(multiplexer_56_out), .sel(in_1[1]));
  Multiplexer #(.enable("false")) multiplexer_57 (
    .in0(multiplexer_25_out), .in1(multiplexer_27_out), .out(multiplexer_57_out), .sel(in_1[1]));
  Multiplexer #(.enable("false")) multiplexer_58 (
    .in0(multiplexer_26_out), .in1(multiplexer_28_out), .out(multiplexer_58_out), .sel(in_1[1]));
  Multiplexer #(.enable("false")) multiplexer_59 (
    .in0(multiplexer_27_out), .in1(multiplexer_29_out), .out(multiplexer_59_out), .sel(in_1[1]));
  Multiplexer #(.enable("false")) multiplexer_60 (
    .in0(multiplexer_28_out), .in1(multiplexer_30_out), .out(multiplexer_60_out), .sel(in_1[1]));
  Multiplexer #(.enable("false")) multiplexer_61 (
    .in0(multiplexer_29_out), .in1(multiplexer_31_out), .out(multiplexer_61_out), .sel(in_1[1]));
  Multiplexer #(.enable("false")) multiplexer_62 (
    .in0(multiplexer_30_out), .in1(multiplexer_32_out), .out(multiplexer_62_out), .sel(in_1[1]));
  Multiplexer #(.enable("false")) multiplexer_63 (
    .in0(multiplexer_31_out), .in1(1'b0), .out(multiplexer_63_out), .sel(in_1[1]));
  Multiplexer #(.enable("false")) multiplexer_64 (
    .in0(multiplexer_32_out), .in1(1'b0), .out(multiplexer_64_out), .sel(in_1[1]));
  Multiplexer #(.enable("false")) multiplexer_65 (
    .in0(multiplexer_33_out), .in1(multiplexer_37_out), .out(multiplexer_65_out), .sel(in_1[2]));
  Multiplexer #(.enable("false")) multiplexer_66 (
    .in0(multiplexer_34_out), .in1(multiplexer_38_out), .out(multiplexer_66_out), .sel(in_1[2]));
  Multiplexer #(.enable("false")) multiplexer_67 (
    .in0(multiplexer_35_out), .in1(multiplexer_39_out), .out(multiplexer_67_out), .sel(in_1[2]));
  Multiplexer #(.enable("false")) multiplexer_68 (
    .in0(multiplexer_36_out), .in1(multiplexer_40_out), .out(multiplexer_68_out), .sel(in_1[2]));
  Multiplexer #(.enable("false")) multiplexer_69 (
    .in0(multiplexer_37_out), .in1(multiplexer_41_out), .out(multiplexer_69_out), .sel(in_1[2]));
  Multiplexer #(.enable("false")) multiplexer_70 (
    .in0(multiplexer_38_out), .in1(multiplexer_42_out), .out(multiplexer_70_out), .sel(in_1[2]));
  Multiplexer #(.enable("false")) multiplexer_71 (
    .in0(multiplexer_39_out), .in1(multiplexer_43_out), .out(multiplexer_71_out), .sel(in_1[2]));
  Multiplexer #(.enable("false")) multiplexer_72 (
    .in0(multiplexer_40_out), .in1(multiplexer_44_out), .out(multiplexer_72_out), .sel(in_1[2]));
  Multiplexer #(.enable("false")) multiplexer_73 (
    .in0(multiplexer_41_out), .in1(multiplexer_45_out), .out(multiplexer_73_out), .sel(in_1[2]));
  Multiplexer #(.enable("false")) multiplexer_74 (
    .in0(multiplexer_42_out), .in1(multiplexer_46_out), .out(multiplexer_74_out), .sel(in_1[2]));
  Multiplexer #(.enable("false")) multiplexer_75 (
    .in0(multiplexer_43_out), .in1(multiplexer_47_out), .out(multiplexer_75_out), .sel(in_1[2]));
  Multiplexer #(.enable("false")) multiplexer_76 (
    .in0(multiplexer_44_out), .in1(multiplexer_48_out), .out(multiplexer_76_out), .sel(in_1[2]));
  Multiplexer #(.enable("false")) multiplexer_77 (
    .in0(multiplexer_45_out), .in1(multiplexer_49_out), .out(multiplexer_77_out), .sel(in_1[2]));
  Multiplexer #(.enable("false")) multiplexer_78 (
    .in0(multiplexer_46_out), .in1(multiplexer_50_out), .out(multiplexer_78_out), .sel(in_1[2]));
  Multiplexer #(.enable("false")) multiplexer_79 (
    .in0(multiplexer_47_out), .in1(multiplexer_51_out), .out(multiplexer_79_out), .sel(in_1[2]));
  Multiplexer #(.enable("false")) multiplexer_80 (
    .in0(multiplexer_48_out), .in1(multiplexer_52_out), .out(multiplexer_80_out), .sel(in_1[2]));
  Multiplexer #(.enable("false")) multiplexer_81 (
    .in0(multiplexer_49_out), .in1(multiplexer_53_out), .out(multiplexer_81_out), .sel(in_1[2]));
  Multiplexer #(.enable("false")) multiplexer_82 (
    .in0(multiplexer_50_out), .in1(multiplexer_54_out), .out(multiplexer_82_out), .sel(in_1[2]));
  Multiplexer #(.enable("false")) multiplexer_83 (
    .in0(multiplexer_51_out), .in1(multiplexer_55_out), .out(multiplexer_83_out), .sel(in_1[2]));
  Multiplexer #(.enable("false")) multiplexer_84 (
    .in0(multiplexer_52_out), .in1(multiplexer_56_out), .out(multiplexer_84_out), .sel(in_1[2]));
  Multiplexer #(.enable("false")) multiplexer_85 (
    .in0(multiplexer_53_out), .in1(multiplexer_57_out), .out(multiplexer_85_out), .sel(in_1[2]));
  Multiplexer #(.enable("false")) multiplexer_86 (
    .in0(multiplexer_54_out), .in1(multiplexer_58_out), .out(multiplexer_86_out), .sel(in_1[2]));
  Multiplexer #(.enable("false")) multiplexer_87 (
    .in0(multiplexer_55_out), .in1(multiplexer_59_out), .out(multiplexer_87_out), .sel(in_1[2]));
  Multiplexer #(.enable("false")) multiplexer_88 (
    .in0(multiplexer_56_out), .in1(multiplexer_60_out), .out(multiplexer_88_out), .sel(in_1[2]));
  Multiplexer #(.enable("false")) multiplexer_89 (
    .in0(multiplexer_57_out), .in1(multiplexer_61_out), .out(multiplexer_89_out), .sel(in_1[2]));
  Multiplexer #(.enable("false")) multiplexer_90 (
    .in0(multiplexer_58_out), .in1(multiplexer_62_out), .out(multiplexer_90_out), .sel(in_1[2]));
  Multiplexer #(.enable("false")) multiplexer_91 (
    .in0(multiplexer_59_out), .in1(multiplexer_63_out), .out(multiplexer_91_out), .sel(in_1[2]));
  Multiplexer #(.enable("false")) multiplexer_92 (
    .in0(multiplexer_60_out), .in1(multiplexer_64_out), .out(multiplexer_92_out), .sel(in_1[2]));
  Multiplexer #(.enable("false")) multiplexer_93 (
    .in0(multiplexer_61_out), .in1(1'b0), .out(multiplexer_93_out), .sel(in_1[2]));
  Multiplexer #(.enable("false")) multiplexer_94 (
    .in0(multiplexer_62_out), .in1(1'b0), .out(multiplexer_94_out), .sel(in_1[2]));
  Multiplexer #(.enable("false")) multiplexer_95 (
    .in0(multiplexer_63_out), .in1(1'b0), .out(multiplexer_95_out), .sel(in_1[2]));
  Multiplexer #(.enable("false")) multiplexer_96 (
    .in0(multiplexer_64_out), .in1(1'b0), .out(multiplexer_96_out), .sel(in_1[2]));
  Multiplexer #(.enable("false")) multiplexer_97 (
    .in0(multiplexer_65_out), .in1(multiplexer_73_out), .out(multiplexer_97_out), .sel(in_1[3]));
  Multiplexer #(.enable("false")) multiplexer_98 (
    .in0(multiplexer_66_out), .in1(multiplexer_74_out), .out(multiplexer_98_out), .sel(in_1[3]));
  Multiplexer #(.enable("false")) multiplexer_99 (
    .in0(multiplexer_67_out), .in1(multiplexer_75_out), .out(multiplexer_99_out), .sel(in_1[3]));
  Multiplexer #(.enable("false")) multiplexer_100 (
    .in0(multiplexer_68_out), .in1(multiplexer_76_out), .out(multiplexer_100_out), .sel(in_1[3]));
  Multiplexer #(.enable("false")) multiplexer_101 (
    .in0(multiplexer_69_out), .in1(multiplexer_77_out), .out(multiplexer_101_out), .sel(in_1[3]));
  Multiplexer #(.enable("false")) multiplexer_102 (
    .in0(multiplexer_70_out), .in1(multiplexer_78_out), .out(multiplexer_102_out), .sel(in_1[3]));
  Multiplexer #(.enable("false")) multiplexer_103 (
    .in0(multiplexer_71_out), .in1(multiplexer_79_out), .out(multiplexer_103_out), .sel(in_1[3]));
  Multiplexer #(.enable("false")) multiplexer_104 (
    .in0(multiplexer_72_out), .in1(multiplexer_80_out), .out(multiplexer_104_out), .sel(in_1[3]));
  Multiplexer #(.enable("false")) multiplexer_105 (
    .in0(multiplexer_73_out), .in1(multiplexer_81_out), .out(multiplexer_105_out), .sel(in_1[3]));
  Multiplexer #(.enable("false")) multiplexer_106 (
    .in0(multiplexer_74_out), .in1(multiplexer_82_out), .out(multiplexer_106_out), .sel(in_1[3]));
  Multiplexer #(.enable("false")) multiplexer_107 (
    .in0(multiplexer_75_out), .in1(multiplexer_83_out), .out(multiplexer_107_out), .sel(in_1[3]));
  Multiplexer #(.enable("false")) multiplexer_108 (
    .in0(multiplexer_76_out), .in1(multiplexer_84_out), .out(multiplexer_108_out), .sel(in_1[3]));
  Multiplexer #(.enable("false")) multiplexer_109 (
    .in0(multiplexer_77_out), .in1(multiplexer_85_out), .out(multiplexer_109_out), .sel(in_1[3]));
  Multiplexer #(.enable("false")) multiplexer_110 (
    .in0(multiplexer_78_out), .in1(multiplexer_86_out), .out(multiplexer_110_out), .sel(in_1[3]));
  Multiplexer #(.enable("false")) multiplexer_111 (
    .in0(multiplexer_79_out), .in1(multiplexer_87_out), .out(multiplexer_111_out), .sel(in_1[3]));
  Multiplexer #(.enable("false")) multiplexer_112 (
    .in0(multiplexer_80_out), .in1(multiplexer_88_out), .out(multiplexer_112_out), .sel(in_1[3]));
  Multiplexer #(.enable("false")) multiplexer_113 (
    .in0(multiplexer_81_out), .in1(multiplexer_89_out), .out(multiplexer_113_out), .sel(in_1[3]));
  Multiplexer #(.enable("false")) multiplexer_114 (
    .in0(multiplexer_82_out), .in1(multiplexer_90_out), .out(multiplexer_114_out), .sel(in_1[3]));
  Multiplexer #(.enable("false")) multiplexer_115 (
    .in0(multiplexer_83_out), .in1(multiplexer_91_out), .out(multiplexer_115_out), .sel(in_1[3]));
  Multiplexer #(.enable("false")) multiplexer_116 (
    .in0(multiplexer_84_out), .in1(multiplexer_92_out), .out(multiplexer_116_out), .sel(in_1[3]));
  Multiplexer #(.enable("false")) multiplexer_117 (
    .in0(multiplexer_85_out), .in1(multiplexer_93_out), .out(multiplexer_117_out), .sel(in_1[3]));
  Multiplexer #(.enable("false")) multiplexer_118 (
    .in0(multiplexer_86_out), .in1(multiplexer_94_out), .out(multiplexer_118_out), .sel(in_1[3]));
  Multiplexer #(.enable("false")) multiplexer_119 (
    .in0(multiplexer_87_out), .in1(multiplexer_95_out), .out(multiplexer_119_out), .sel(in_1[3]));
  Multiplexer #(.enable("false")) multiplexer_120 (
    .in0(multiplexer_88_out), .in1(multiplexer_96_out), .out(multiplexer_120_out), .sel(in_1[3]));
  Multiplexer #(.enable("false")) multiplexer_121 (
    .in0(multiplexer_89_out), .in1(1'b0), .out(multiplexer_121_out), .sel(in_1[3]));
  Multiplexer #(.enable("false")) multiplexer_122 (
    .in0(multiplexer_90_out), .in1(1'b0), .out(multiplexer_122_out), .sel(in_1[3]));
  Multiplexer #(.enable("false")) multiplexer_123 (
    .in0(multiplexer_91_out), .in1(1'b0), .out(multiplexer_123_out), .sel(in_1[3]));
  Multiplexer #(.enable("false")) multiplexer_124 (
    .in0(multiplexer_92_out), .in1(1'b0), .out(multiplexer_124_out), .sel(in_1[3]));
  Multiplexer #(.enable("false")) multiplexer_125 (
    .in0(multiplexer_93_out), .in1(1'b0), .out(multiplexer_125_out), .sel(in_1[3]));
  Multiplexer #(.enable("false")) multiplexer_126 (
    .in0(multiplexer_94_out), .in1(1'b0), .out(multiplexer_126_out), .sel(in_1[3]));
  Multiplexer #(.enable("false")) multiplexer_127 (
    .in0(multiplexer_95_out), .in1(1'b0), .out(multiplexer_127_out), .sel(in_1[3]));
  Multiplexer #(.enable("false")) multiplexer_128 (
    .in0(multiplexer_96_out), .in1(1'b0), .out(multiplexer_128_out), .sel(in_1[3]));
  Multiplexer #(.enable("false")) multiplexer_129 (
    .in0(multiplexer_97_out), .in1(multiplexer_113_out), .out(out_3[31]), .sel(in_1[4]));
  Multiplexer #(.enable("false")) multiplexer_130 (
    .in0(multiplexer_98_out), .in1(multiplexer_114_out), .out(out_3[30]), .sel(in_1[4]));
  Multiplexer #(.enable("false")) multiplexer_131 (
    .in0(multiplexer_99_out), .in1(multiplexer_115_out), .out(out_3[29]), .sel(in_1[4]));
  Multiplexer #(.enable("false")) multiplexer_132 (
    .in0(multiplexer_100_out), .in1(multiplexer_116_out), .out(out_3[28]), .sel(in_1[4]));
  Multiplexer #(.enable("false")) multiplexer_133 (
    .in0(multiplexer_101_out), .in1(multiplexer_117_out), .out(out_3[27]), .sel(in_1[4]));
  Multiplexer #(.enable("false")) multiplexer_134 (
    .in0(multiplexer_102_out), .in1(multiplexer_118_out), .out(out_3[26]), .sel(in_1[4]));
  Multiplexer #(.enable("false")) multiplexer_135 (
    .in0(multiplexer_103_out), .in1(multiplexer_119_out), .out(out_3[25]), .sel(in_1[4]));
  Multiplexer #(.enable("false")) multiplexer_136 (
    .in0(multiplexer_104_out), .in1(multiplexer_120_out), .out(out_3[24]), .sel(in_1[4]));
  Multiplexer #(.enable("false")) multiplexer_137 (
    .in0(multiplexer_105_out), .in1(multiplexer_121_out), .out(out_3[23]), .sel(in_1[4]));
  Multiplexer #(.enable("false")) multiplexer_138 (
    .in0(multiplexer_106_out), .in1(multiplexer_122_out), .out(out_3[22]), .sel(in_1[4]));
  Multiplexer #(.enable("false")) multiplexer_139 (
    .in0(multiplexer_107_out), .in1(multiplexer_123_out), .out(out_3[21]), .sel(in_1[4]));
  Multiplexer #(.enable("false")) multiplexer_140 (
    .in0(multiplexer_108_out), .in1(multiplexer_124_out), .out(out_3[20]), .sel(in_1[4]));
  Multiplexer #(.enable("false")) multiplexer_141 (
    .in0(multiplexer_109_out), .in1(multiplexer_125_out), .out(out_3[19]), .sel(in_1[4]));
  Multiplexer #(.enable("false")) multiplexer_142 (
    .in0(multiplexer_110_out), .in1(multiplexer_126_out), .out(out_3[18]), .sel(in_1[4]));
  Multiplexer #(.enable("false")) multiplexer_143 (
    .in0(multiplexer_111_out), .in1(multiplexer_127_out), .out(out_3[17]), .sel(in_1[4]));
  Multiplexer #(.enable("false")) multiplexer_144 (
    .in0(multiplexer_112_out), .in1(multiplexer_128_out), .out(out_3[16]), .sel(in_1[4]));
  Multiplexer #(.enable("false")) multiplexer_145 (
    .in0(multiplexer_113_out), .in1(1'b0), .out(out_3[15]), .sel(in_1[4]));
  Multiplexer #(.enable("false")) multiplexer_146 (
    .in0(multiplexer_114_out), .in1(1'b0), .out(out_3[14]), .sel(in_1[4]));
  Multiplexer #(.enable("false")) multiplexer_147 (
    .in0(multiplexer_115_out), .in1(1'b0), .out(out_3[13]), .sel(in_1[4]));
  Multiplexer #(.enable("false")) multiplexer_148 (
    .in0(multiplexer_116_out), .in1(1'b0), .out(out_3[12]), .sel(in_1[4]));
  Multiplexer #(.enable("false")) multiplexer_149 (
    .in0(multiplexer_117_out), .in1(1'b0), .out(out_3[11]), .sel(in_1[4]));
  Multiplexer #(.enable("false")) multiplexer_150 (
    .in0(multiplexer_118_out), .in1(1'b0), .out(out_3[10]), .sel(in_1[4]));
  Multiplexer #(.enable("false")) multiplexer_151 (
    .in0(multiplexer_119_out), .in1(1'b0), .out(out_3[9]), .sel(in_1[4]));
  Multiplexer #(.enable("false")) multiplexer_152 (
    .in0(multiplexer_120_out), .in1(1'b0), .out(out_3[8]), .sel(in_1[4]));
  Multiplexer #(.enable("false")) multiplexer_153 (
    .in0(multiplexer_121_out), .in1(1'b0), .out(out_3[7]), .sel(in_1[4]));
  Multiplexer #(.enable("false")) multiplexer_154 (
    .in0(multiplexer_122_out), .in1(1'b0), .out(out_3[6]), .sel(in_1[4]));
  Multiplexer #(.enable("false")) multiplexer_155 (
    .in0(multiplexer_123_out), .in1(1'b0), .out(out_3[5]), .sel(in_1[4]));
  Multiplexer #(.enable("false")) multiplexer_156 (
    .in0(multiplexer_124_out), .in1(1'b0), .out(out_3[4]), .sel(in_1[4]));
  Multiplexer #(.enable("false")) multiplexer_157 (
    .in0(multiplexer_125_out), .in1(1'b0), .out(out_3[3]), .sel(in_1[4]));
  Multiplexer #(.enable("false")) multiplexer_158 (
    .in0(multiplexer_126_out), .in1(1'b0), .out(out_3[2]), .sel(in_1[4]));
  Multiplexer #(.enable("false")) multiplexer_159 (
    .in0(multiplexer_127_out), .in1(1'b0), .out(out_3[1]), .sel(in_1[4]));
  Multiplexer #(.enable("false")) multiplexer_160 (
    .in0(multiplexer_128_out), .in1(1'b0), .out(out_3[0]), .sel(in_1[4]));

  // Notes on the sheet:
  //   5
  //   10
  //   15
  //   20
  //   25
  //   30
  //   5
  //   10
  //   15
  //   20
  //   25
  //   30
  //   5
  //   10
  //   15
  //   20
  //   25
  //   30
  //   5
  //   5
  //   10
  //   10
  //   15
  //   15
  //   20
  //   20
  //   25
  //   25
  //   30
  //   30
  //   5
  //   10
  //   15
  //   20
  //   25
  //   30
endmodule

module SRL (
  input  [4:0] in_1,
  input  [31:0] in_2,
  output [31:0] out_3
);

  wire multiplexer_1_out, multiplexer_2_out, multiplexer_3_out, multiplexer_4_out, multiplexer_5_out,
       multiplexer_6_out, multiplexer_7_out, multiplexer_8_out, multiplexer_9_out, multiplexer_10_out,
       multiplexer_11_out, multiplexer_12_out, multiplexer_13_out, multiplexer_14_out, multiplexer_15_out,
       multiplexer_16_out, multiplexer_17_out, multiplexer_18_out, multiplexer_19_out, multiplexer_20_out,
       multiplexer_21_out, multiplexer_22_out, multiplexer_23_out, multiplexer_24_out, multiplexer_25_out,
       multiplexer_26_out, multiplexer_27_out, multiplexer_28_out, multiplexer_29_out, multiplexer_30_out,
       multiplexer_31_out, multiplexer_32_out, multiplexer_33_out, multiplexer_34_out, multiplexer_35_out,
       multiplexer_36_out, multiplexer_37_out, multiplexer_38_out, multiplexer_39_out, multiplexer_40_out,
       multiplexer_41_out, multiplexer_42_out, multiplexer_43_out, multiplexer_44_out, multiplexer_45_out,
       multiplexer_46_out, multiplexer_47_out, multiplexer_48_out, multiplexer_49_out, multiplexer_50_out,
       multiplexer_51_out, multiplexer_52_out, multiplexer_53_out, multiplexer_54_out, multiplexer_55_out,
       multiplexer_56_out, multiplexer_57_out, multiplexer_58_out, multiplexer_59_out, multiplexer_60_out,
       multiplexer_61_out, multiplexer_62_out, multiplexer_63_out, multiplexer_64_out, multiplexer_65_out,
       multiplexer_66_out, multiplexer_67_out, multiplexer_68_out, multiplexer_69_out, multiplexer_70_out,
       multiplexer_71_out, multiplexer_72_out, multiplexer_73_out, multiplexer_74_out, multiplexer_75_out,
       multiplexer_76_out, multiplexer_77_out, multiplexer_78_out, multiplexer_79_out, multiplexer_80_out,
       multiplexer_81_out, multiplexer_82_out, multiplexer_83_out, multiplexer_84_out, multiplexer_85_out,
       multiplexer_86_out, multiplexer_87_out, multiplexer_88_out, multiplexer_89_out, multiplexer_90_out,
       multiplexer_91_out, multiplexer_92_out, multiplexer_93_out, multiplexer_94_out, multiplexer_95_out,
       multiplexer_96_out, multiplexer_97_out, multiplexer_98_out, multiplexer_99_out, multiplexer_100_out,
       multiplexer_101_out, multiplexer_102_out, multiplexer_103_out, multiplexer_104_out,
       multiplexer_105_out, multiplexer_106_out, multiplexer_107_out, multiplexer_108_out,
       multiplexer_109_out, multiplexer_110_out, multiplexer_111_out, multiplexer_112_out,
       multiplexer_113_out, multiplexer_114_out, multiplexer_115_out, multiplexer_116_out,
       multiplexer_117_out, multiplexer_118_out, multiplexer_119_out, multiplexer_120_out,
       multiplexer_121_out, multiplexer_122_out, multiplexer_123_out, multiplexer_124_out,
       multiplexer_125_out, multiplexer_126_out, multiplexer_127_out, multiplexer_128_out;

  Multiplexer #(.enable("false")) multiplexer_1 (.in0(in_2[0]), .in1(in_2[1]), .out(multiplexer_1_out), .sel(in_1[0]));
  Multiplexer #(.enable("false")) multiplexer_2 (.in0(in_2[1]), .in1(in_2[2]), .out(multiplexer_2_out), .sel(in_1[0]));
  Multiplexer #(.enable("false")) multiplexer_3 (.in0(in_2[2]), .in1(in_2[3]), .out(multiplexer_3_out), .sel(in_1[0]));
  Multiplexer #(.enable("false")) multiplexer_4 (.in0(in_2[3]), .in1(in_2[4]), .out(multiplexer_4_out), .sel(in_1[0]));
  Multiplexer #(.enable("false")) multiplexer_5 (.in0(in_2[4]), .in1(in_2[5]), .out(multiplexer_5_out), .sel(in_1[0]));
  Multiplexer #(.enable("false")) multiplexer_6 (.in0(in_2[5]), .in1(in_2[6]), .out(multiplexer_6_out), .sel(in_1[0]));
  Multiplexer #(.enable("false")) multiplexer_7 (.in0(in_2[6]), .in1(in_2[7]), .out(multiplexer_7_out), .sel(in_1[0]));
  Multiplexer #(.enable("false")) multiplexer_8 (.in0(in_2[7]), .in1(in_2[8]), .out(multiplexer_8_out), .sel(in_1[0]));
  Multiplexer #(.enable("false")) multiplexer_9 (.in0(in_2[8]), .in1(in_2[9]), .out(multiplexer_9_out), .sel(in_1[0]));
  Multiplexer #(.enable("false")) multiplexer_10 (
    .in0(in_2[9]), .in1(in_2[10]), .out(multiplexer_10_out), .sel(in_1[0]));
  Multiplexer #(.enable("false")) multiplexer_11 (
    .in0(in_2[10]), .in1(in_2[11]), .out(multiplexer_11_out), .sel(in_1[0]));
  Multiplexer #(.enable("false")) multiplexer_12 (
    .in0(in_2[11]), .in1(in_2[12]), .out(multiplexer_12_out), .sel(in_1[0]));
  Multiplexer #(.enable("false")) multiplexer_13 (
    .in0(in_2[12]), .in1(in_2[13]), .out(multiplexer_13_out), .sel(in_1[0]));
  Multiplexer #(.enable("false")) multiplexer_14 (
    .in0(in_2[13]), .in1(in_2[14]), .out(multiplexer_14_out), .sel(in_1[0]));
  Multiplexer #(.enable("false")) multiplexer_15 (
    .in0(in_2[14]), .in1(in_2[15]), .out(multiplexer_15_out), .sel(in_1[0]));
  Multiplexer #(.enable("false")) multiplexer_16 (
    .in0(in_2[15]), .in1(in_2[16]), .out(multiplexer_16_out), .sel(in_1[0]));
  Multiplexer #(.enable("false")) multiplexer_17 (
    .in0(in_2[16]), .in1(in_2[17]), .out(multiplexer_17_out), .sel(in_1[0]));
  Multiplexer #(.enable("false")) multiplexer_18 (
    .in0(in_2[17]), .in1(in_2[18]), .out(multiplexer_18_out), .sel(in_1[0]));
  Multiplexer #(.enable("false")) multiplexer_19 (
    .in0(in_2[18]), .in1(in_2[19]), .out(multiplexer_19_out), .sel(in_1[0]));
  Multiplexer #(.enable("false")) multiplexer_20 (
    .in0(in_2[19]), .in1(in_2[20]), .out(multiplexer_20_out), .sel(in_1[0]));
  Multiplexer #(.enable("false")) multiplexer_21 (
    .in0(in_2[20]), .in1(in_2[21]), .out(multiplexer_21_out), .sel(in_1[0]));
  Multiplexer #(.enable("false")) multiplexer_22 (
    .in0(in_2[21]), .in1(in_2[22]), .out(multiplexer_22_out), .sel(in_1[0]));
  Multiplexer #(.enable("false")) multiplexer_23 (
    .in0(in_2[22]), .in1(in_2[23]), .out(multiplexer_23_out), .sel(in_1[0]));
  Multiplexer #(.enable("false")) multiplexer_24 (
    .in0(in_2[23]), .in1(in_2[24]), .out(multiplexer_24_out), .sel(in_1[0]));
  Multiplexer #(.enable("false")) multiplexer_25 (
    .in0(in_2[24]), .in1(in_2[25]), .out(multiplexer_25_out), .sel(in_1[0]));
  Multiplexer #(.enable("false")) multiplexer_26 (
    .in0(in_2[25]), .in1(in_2[26]), .out(multiplexer_26_out), .sel(in_1[0]));
  Multiplexer #(.enable("false")) multiplexer_27 (
    .in0(in_2[26]), .in1(in_2[27]), .out(multiplexer_27_out), .sel(in_1[0]));
  Multiplexer #(.enable("false")) multiplexer_28 (
    .in0(in_2[27]), .in1(in_2[28]), .out(multiplexer_28_out), .sel(in_1[0]));
  Multiplexer #(.enable("false")) multiplexer_29 (
    .in0(in_2[28]), .in1(in_2[29]), .out(multiplexer_29_out), .sel(in_1[0]));
  Multiplexer #(.enable("false")) multiplexer_30 (
    .in0(in_2[29]), .in1(in_2[30]), .out(multiplexer_30_out), .sel(in_1[0]));
  Multiplexer #(.enable("false")) multiplexer_31 (
    .in0(in_2[30]), .in1(in_2[31]), .out(multiplexer_31_out), .sel(in_1[0]));
  Multiplexer #(.enable("false")) multiplexer_32 (.in0(in_2[31]), .in1(1'b0), .out(multiplexer_32_out), .sel(in_1[0]));
  Multiplexer #(.enable("false")) multiplexer_33 (
    .in0(multiplexer_1_out), .in1(multiplexer_3_out), .out(multiplexer_33_out), .sel(in_1[1]));
  Multiplexer #(.enable("false")) multiplexer_34 (
    .in0(multiplexer_2_out), .in1(multiplexer_4_out), .out(multiplexer_34_out), .sel(in_1[1]));
  Multiplexer #(.enable("false")) multiplexer_35 (
    .in0(multiplexer_3_out), .in1(multiplexer_5_out), .out(multiplexer_35_out), .sel(in_1[1]));
  Multiplexer #(.enable("false")) multiplexer_36 (
    .in0(multiplexer_4_out), .in1(multiplexer_6_out), .out(multiplexer_36_out), .sel(in_1[1]));
  Multiplexer #(.enable("false")) multiplexer_37 (
    .in0(multiplexer_5_out), .in1(multiplexer_7_out), .out(multiplexer_37_out), .sel(in_1[1]));
  Multiplexer #(.enable("false")) multiplexer_38 (
    .in0(multiplexer_6_out), .in1(multiplexer_8_out), .out(multiplexer_38_out), .sel(in_1[1]));
  Multiplexer #(.enable("false")) multiplexer_39 (
    .in0(multiplexer_7_out), .in1(multiplexer_9_out), .out(multiplexer_39_out), .sel(in_1[1]));
  Multiplexer #(.enable("false")) multiplexer_40 (
    .in0(multiplexer_8_out), .in1(multiplexer_10_out), .out(multiplexer_40_out), .sel(in_1[1]));
  Multiplexer #(.enable("false")) multiplexer_41 (
    .in0(multiplexer_9_out), .in1(multiplexer_11_out), .out(multiplexer_41_out), .sel(in_1[1]));
  Multiplexer #(.enable("false")) multiplexer_42 (
    .in0(multiplexer_10_out), .in1(multiplexer_12_out), .out(multiplexer_42_out), .sel(in_1[1]));
  Multiplexer #(.enable("false")) multiplexer_43 (
    .in0(multiplexer_11_out), .in1(multiplexer_13_out), .out(multiplexer_43_out), .sel(in_1[1]));
  Multiplexer #(.enable("false")) multiplexer_44 (
    .in0(multiplexer_12_out), .in1(multiplexer_14_out), .out(multiplexer_44_out), .sel(in_1[1]));
  Multiplexer #(.enable("false")) multiplexer_45 (
    .in0(multiplexer_13_out), .in1(multiplexer_15_out), .out(multiplexer_45_out), .sel(in_1[1]));
  Multiplexer #(.enable("false")) multiplexer_46 (
    .in0(multiplexer_14_out), .in1(multiplexer_16_out), .out(multiplexer_46_out), .sel(in_1[1]));
  Multiplexer #(.enable("false")) multiplexer_47 (
    .in0(multiplexer_15_out), .in1(multiplexer_17_out), .out(multiplexer_47_out), .sel(in_1[1]));
  Multiplexer #(.enable("false")) multiplexer_48 (
    .in0(multiplexer_16_out), .in1(multiplexer_18_out), .out(multiplexer_48_out), .sel(in_1[1]));
  Multiplexer #(.enable("false")) multiplexer_49 (
    .in0(multiplexer_17_out), .in1(multiplexer_19_out), .out(multiplexer_49_out), .sel(in_1[1]));
  Multiplexer #(.enable("false")) multiplexer_50 (
    .in0(multiplexer_18_out), .in1(multiplexer_20_out), .out(multiplexer_50_out), .sel(in_1[1]));
  Multiplexer #(.enable("false")) multiplexer_51 (
    .in0(multiplexer_19_out), .in1(multiplexer_21_out), .out(multiplexer_51_out), .sel(in_1[1]));
  Multiplexer #(.enable("false")) multiplexer_52 (
    .in0(multiplexer_20_out), .in1(multiplexer_22_out), .out(multiplexer_52_out), .sel(in_1[1]));
  Multiplexer #(.enable("false")) multiplexer_53 (
    .in0(multiplexer_21_out), .in1(multiplexer_23_out), .out(multiplexer_53_out), .sel(in_1[1]));
  Multiplexer #(.enable("false")) multiplexer_54 (
    .in0(multiplexer_22_out), .in1(multiplexer_24_out), .out(multiplexer_54_out), .sel(in_1[1]));
  Multiplexer #(.enable("false")) multiplexer_55 (
    .in0(multiplexer_23_out), .in1(multiplexer_25_out), .out(multiplexer_55_out), .sel(in_1[1]));
  Multiplexer #(.enable("false")) multiplexer_56 (
    .in0(multiplexer_24_out), .in1(multiplexer_26_out), .out(multiplexer_56_out), .sel(in_1[1]));
  Multiplexer #(.enable("false")) multiplexer_57 (
    .in0(multiplexer_25_out), .in1(multiplexer_27_out), .out(multiplexer_57_out), .sel(in_1[1]));
  Multiplexer #(.enable("false")) multiplexer_58 (
    .in0(multiplexer_26_out), .in1(multiplexer_28_out), .out(multiplexer_58_out), .sel(in_1[1]));
  Multiplexer #(.enable("false")) multiplexer_59 (
    .in0(multiplexer_27_out), .in1(multiplexer_29_out), .out(multiplexer_59_out), .sel(in_1[1]));
  Multiplexer #(.enable("false")) multiplexer_60 (
    .in0(multiplexer_28_out), .in1(multiplexer_30_out), .out(multiplexer_60_out), .sel(in_1[1]));
  Multiplexer #(.enable("false")) multiplexer_61 (
    .in0(multiplexer_29_out), .in1(multiplexer_31_out), .out(multiplexer_61_out), .sel(in_1[1]));
  Multiplexer #(.enable("false")) multiplexer_62 (
    .in0(multiplexer_30_out), .in1(multiplexer_32_out), .out(multiplexer_62_out), .sel(in_1[1]));
  Multiplexer #(.enable("false")) multiplexer_63 (
    .in0(multiplexer_31_out), .in1(1'b0), .out(multiplexer_63_out), .sel(in_1[1]));
  Multiplexer #(.enable("false")) multiplexer_64 (
    .in0(multiplexer_32_out), .in1(1'b0), .out(multiplexer_64_out), .sel(in_1[1]));
  Multiplexer #(.enable("false")) multiplexer_65 (
    .in0(multiplexer_33_out), .in1(multiplexer_37_out), .out(multiplexer_65_out), .sel(in_1[2]));
  Multiplexer #(.enable("false")) multiplexer_66 (
    .in0(multiplexer_34_out), .in1(multiplexer_38_out), .out(multiplexer_66_out), .sel(in_1[2]));
  Multiplexer #(.enable("false")) multiplexer_67 (
    .in0(multiplexer_35_out), .in1(multiplexer_39_out), .out(multiplexer_67_out), .sel(in_1[2]));
  Multiplexer #(.enable("false")) multiplexer_68 (
    .in0(multiplexer_36_out), .in1(multiplexer_40_out), .out(multiplexer_68_out), .sel(in_1[2]));
  Multiplexer #(.enable("false")) multiplexer_69 (
    .in0(multiplexer_37_out), .in1(multiplexer_41_out), .out(multiplexer_69_out), .sel(in_1[2]));
  Multiplexer #(.enable("false")) multiplexer_70 (
    .in0(multiplexer_38_out), .in1(multiplexer_42_out), .out(multiplexer_70_out), .sel(in_1[2]));
  Multiplexer #(.enable("false")) multiplexer_71 (
    .in0(multiplexer_39_out), .in1(multiplexer_43_out), .out(multiplexer_71_out), .sel(in_1[2]));
  Multiplexer #(.enable("false")) multiplexer_72 (
    .in0(multiplexer_40_out), .in1(multiplexer_44_out), .out(multiplexer_72_out), .sel(in_1[2]));
  Multiplexer #(.enable("false")) multiplexer_73 (
    .in0(multiplexer_41_out), .in1(multiplexer_45_out), .out(multiplexer_73_out), .sel(in_1[2]));
  Multiplexer #(.enable("false")) multiplexer_74 (
    .in0(multiplexer_42_out), .in1(multiplexer_46_out), .out(multiplexer_74_out), .sel(in_1[2]));
  Multiplexer #(.enable("false")) multiplexer_75 (
    .in0(multiplexer_43_out), .in1(multiplexer_47_out), .out(multiplexer_75_out), .sel(in_1[2]));
  Multiplexer #(.enable("false")) multiplexer_76 (
    .in0(multiplexer_44_out), .in1(multiplexer_48_out), .out(multiplexer_76_out), .sel(in_1[2]));
  Multiplexer #(.enable("false")) multiplexer_77 (
    .in0(multiplexer_45_out), .in1(multiplexer_49_out), .out(multiplexer_77_out), .sel(in_1[2]));
  Multiplexer #(.enable("false")) multiplexer_78 (
    .in0(multiplexer_46_out), .in1(multiplexer_50_out), .out(multiplexer_78_out), .sel(in_1[2]));
  Multiplexer #(.enable("false")) multiplexer_79 (
    .in0(multiplexer_47_out), .in1(multiplexer_51_out), .out(multiplexer_79_out), .sel(in_1[2]));
  Multiplexer #(.enable("false")) multiplexer_80 (
    .in0(multiplexer_48_out), .in1(multiplexer_52_out), .out(multiplexer_80_out), .sel(in_1[2]));
  Multiplexer #(.enable("false")) multiplexer_81 (
    .in0(multiplexer_49_out), .in1(multiplexer_53_out), .out(multiplexer_81_out), .sel(in_1[2]));
  Multiplexer #(.enable("false")) multiplexer_82 (
    .in0(multiplexer_50_out), .in1(multiplexer_54_out), .out(multiplexer_82_out), .sel(in_1[2]));
  Multiplexer #(.enable("false")) multiplexer_83 (
    .in0(multiplexer_51_out), .in1(multiplexer_55_out), .out(multiplexer_83_out), .sel(in_1[2]));
  Multiplexer #(.enable("false")) multiplexer_84 (
    .in0(multiplexer_52_out), .in1(multiplexer_56_out), .out(multiplexer_84_out), .sel(in_1[2]));
  Multiplexer #(.enable("false")) multiplexer_85 (
    .in0(multiplexer_53_out), .in1(multiplexer_57_out), .out(multiplexer_85_out), .sel(in_1[2]));
  Multiplexer #(.enable("false")) multiplexer_86 (
    .in0(multiplexer_54_out), .in1(multiplexer_58_out), .out(multiplexer_86_out), .sel(in_1[2]));
  Multiplexer #(.enable("false")) multiplexer_87 (
    .in0(multiplexer_55_out), .in1(multiplexer_59_out), .out(multiplexer_87_out), .sel(in_1[2]));
  Multiplexer #(.enable("false")) multiplexer_88 (
    .in0(multiplexer_56_out), .in1(multiplexer_60_out), .out(multiplexer_88_out), .sel(in_1[2]));
  Multiplexer #(.enable("false")) multiplexer_89 (
    .in0(multiplexer_57_out), .in1(multiplexer_61_out), .out(multiplexer_89_out), .sel(in_1[2]));
  Multiplexer #(.enable("false")) multiplexer_90 (
    .in0(multiplexer_58_out), .in1(multiplexer_62_out), .out(multiplexer_90_out), .sel(in_1[2]));
  Multiplexer #(.enable("false")) multiplexer_91 (
    .in0(multiplexer_59_out), .in1(multiplexer_63_out), .out(multiplexer_91_out), .sel(in_1[2]));
  Multiplexer #(.enable("false")) multiplexer_92 (
    .in0(multiplexer_60_out), .in1(multiplexer_64_out), .out(multiplexer_92_out), .sel(in_1[2]));
  Multiplexer #(.enable("false")) multiplexer_93 (
    .in0(multiplexer_61_out), .in1(1'b0), .out(multiplexer_93_out), .sel(in_1[2]));
  Multiplexer #(.enable("false")) multiplexer_94 (
    .in0(multiplexer_62_out), .in1(1'b0), .out(multiplexer_94_out), .sel(in_1[2]));
  Multiplexer #(.enable("false")) multiplexer_95 (
    .in0(multiplexer_63_out), .in1(1'b0), .out(multiplexer_95_out), .sel(in_1[2]));
  Multiplexer #(.enable("false")) multiplexer_96 (
    .in0(multiplexer_64_out), .in1(1'b0), .out(multiplexer_96_out), .sel(in_1[2]));
  Multiplexer #(.enable("false")) multiplexer_97 (
    .in0(multiplexer_65_out), .in1(multiplexer_73_out), .out(multiplexer_97_out), .sel(in_1[3]));
  Multiplexer #(.enable("false")) multiplexer_98 (
    .in0(multiplexer_66_out), .in1(multiplexer_74_out), .out(multiplexer_98_out), .sel(in_1[3]));
  Multiplexer #(.enable("false")) multiplexer_99 (
    .in0(multiplexer_67_out), .in1(multiplexer_75_out), .out(multiplexer_99_out), .sel(in_1[3]));
  Multiplexer #(.enable("false")) multiplexer_100 (
    .in0(multiplexer_68_out), .in1(multiplexer_76_out), .out(multiplexer_100_out), .sel(in_1[3]));
  Multiplexer #(.enable("false")) multiplexer_101 (
    .in0(multiplexer_69_out), .in1(multiplexer_77_out), .out(multiplexer_101_out), .sel(in_1[3]));
  Multiplexer #(.enable("false")) multiplexer_102 (
    .in0(multiplexer_70_out), .in1(multiplexer_78_out), .out(multiplexer_102_out), .sel(in_1[3]));
  Multiplexer #(.enable("false")) multiplexer_103 (
    .in0(multiplexer_71_out), .in1(multiplexer_79_out), .out(multiplexer_103_out), .sel(in_1[3]));
  Multiplexer #(.enable("false")) multiplexer_104 (
    .in0(multiplexer_72_out), .in1(multiplexer_80_out), .out(multiplexer_104_out), .sel(in_1[3]));
  Multiplexer #(.enable("false")) multiplexer_105 (
    .in0(multiplexer_73_out), .in1(multiplexer_81_out), .out(multiplexer_105_out), .sel(in_1[3]));
  Multiplexer #(.enable("false")) multiplexer_106 (
    .in0(multiplexer_74_out), .in1(multiplexer_82_out), .out(multiplexer_106_out), .sel(in_1[3]));
  Multiplexer #(.enable("false")) multiplexer_107 (
    .in0(multiplexer_75_out), .in1(multiplexer_83_out), .out(multiplexer_107_out), .sel(in_1[3]));
  Multiplexer #(.enable("false")) multiplexer_108 (
    .in0(multiplexer_76_out), .in1(multiplexer_84_out), .out(multiplexer_108_out), .sel(in_1[3]));
  Multiplexer #(.enable("false")) multiplexer_109 (
    .in0(multiplexer_77_out), .in1(multiplexer_85_out), .out(multiplexer_109_out), .sel(in_1[3]));
  Multiplexer #(.enable("false")) multiplexer_110 (
    .in0(multiplexer_78_out), .in1(multiplexer_86_out), .out(multiplexer_110_out), .sel(in_1[3]));
  Multiplexer #(.enable("false")) multiplexer_111 (
    .in0(multiplexer_79_out), .in1(multiplexer_87_out), .out(multiplexer_111_out), .sel(in_1[3]));
  Multiplexer #(.enable("false")) multiplexer_112 (
    .in0(multiplexer_80_out), .in1(multiplexer_88_out), .out(multiplexer_112_out), .sel(in_1[3]));
  Multiplexer #(.enable("false")) multiplexer_113 (
    .in0(multiplexer_81_out), .in1(multiplexer_89_out), .out(multiplexer_113_out), .sel(in_1[3]));
  Multiplexer #(.enable("false")) multiplexer_114 (
    .in0(multiplexer_82_out), .in1(multiplexer_90_out), .out(multiplexer_114_out), .sel(in_1[3]));
  Multiplexer #(.enable("false")) multiplexer_115 (
    .in0(multiplexer_83_out), .in1(multiplexer_91_out), .out(multiplexer_115_out), .sel(in_1[3]));
  Multiplexer #(.enable("false")) multiplexer_116 (
    .in0(multiplexer_84_out), .in1(multiplexer_92_out), .out(multiplexer_116_out), .sel(in_1[3]));
  Multiplexer #(.enable("false")) multiplexer_117 (
    .in0(multiplexer_85_out), .in1(multiplexer_93_out), .out(multiplexer_117_out), .sel(in_1[3]));
  Multiplexer #(.enable("false")) multiplexer_118 (
    .in0(multiplexer_86_out), .in1(multiplexer_94_out), .out(multiplexer_118_out), .sel(in_1[3]));
  Multiplexer #(.enable("false")) multiplexer_119 (
    .in0(multiplexer_87_out), .in1(multiplexer_95_out), .out(multiplexer_119_out), .sel(in_1[3]));
  Multiplexer #(.enable("false")) multiplexer_120 (
    .in0(multiplexer_88_out), .in1(multiplexer_96_out), .out(multiplexer_120_out), .sel(in_1[3]));
  Multiplexer #(.enable("false")) multiplexer_121 (
    .in0(multiplexer_89_out), .in1(1'b0), .out(multiplexer_121_out), .sel(in_1[3]));
  Multiplexer #(.enable("false")) multiplexer_122 (
    .in0(multiplexer_90_out), .in1(1'b0), .out(multiplexer_122_out), .sel(in_1[3]));
  Multiplexer #(.enable("false")) multiplexer_123 (
    .in0(multiplexer_91_out), .in1(1'b0), .out(multiplexer_123_out), .sel(in_1[3]));
  Multiplexer #(.enable("false")) multiplexer_124 (
    .in0(multiplexer_92_out), .in1(1'b0), .out(multiplexer_124_out), .sel(in_1[3]));
  Multiplexer #(.enable("false")) multiplexer_125 (
    .in0(multiplexer_93_out), .in1(1'b0), .out(multiplexer_125_out), .sel(in_1[3]));
  Multiplexer #(.enable("false")) multiplexer_126 (
    .in0(multiplexer_94_out), .in1(1'b0), .out(multiplexer_126_out), .sel(in_1[3]));
  Multiplexer #(.enable("false")) multiplexer_127 (
    .in0(multiplexer_95_out), .in1(1'b0), .out(multiplexer_127_out), .sel(in_1[3]));
  Multiplexer #(.enable("false")) multiplexer_128 (
    .in0(multiplexer_96_out), .in1(1'b0), .out(multiplexer_128_out), .sel(in_1[3]));
  Multiplexer #(.enable("false")) multiplexer_129 (
    .in0(multiplexer_97_out), .in1(multiplexer_113_out), .out(out_3[0]), .sel(in_1[4]));
  Multiplexer #(.enable("false")) multiplexer_130 (
    .in0(multiplexer_98_out), .in1(multiplexer_114_out), .out(out_3[1]), .sel(in_1[4]));
  Multiplexer #(.enable("false")) multiplexer_131 (
    .in0(multiplexer_99_out), .in1(multiplexer_115_out), .out(out_3[2]), .sel(in_1[4]));
  Multiplexer #(.enable("false")) multiplexer_132 (
    .in0(multiplexer_100_out), .in1(multiplexer_116_out), .out(out_3[3]), .sel(in_1[4]));
  Multiplexer #(.enable("false")) multiplexer_133 (
    .in0(multiplexer_101_out), .in1(multiplexer_117_out), .out(out_3[4]), .sel(in_1[4]));
  Multiplexer #(.enable("false")) multiplexer_134 (
    .in0(multiplexer_102_out), .in1(multiplexer_118_out), .out(out_3[5]), .sel(in_1[4]));
  Multiplexer #(.enable("false")) multiplexer_135 (
    .in0(multiplexer_103_out), .in1(multiplexer_119_out), .out(out_3[6]), .sel(in_1[4]));
  Multiplexer #(.enable("false")) multiplexer_136 (
    .in0(multiplexer_104_out), .in1(multiplexer_120_out), .out(out_3[7]), .sel(in_1[4]));
  Multiplexer #(.enable("false")) multiplexer_137 (
    .in0(multiplexer_105_out), .in1(multiplexer_121_out), .out(out_3[8]), .sel(in_1[4]));
  Multiplexer #(.enable("false")) multiplexer_138 (
    .in0(multiplexer_106_out), .in1(multiplexer_122_out), .out(out_3[9]), .sel(in_1[4]));
  Multiplexer #(.enable("false")) multiplexer_139 (
    .in0(multiplexer_107_out), .in1(multiplexer_123_out), .out(out_3[10]), .sel(in_1[4]));
  Multiplexer #(.enable("false")) multiplexer_140 (
    .in0(multiplexer_108_out), .in1(multiplexer_124_out), .out(out_3[11]), .sel(in_1[4]));
  Multiplexer #(.enable("false")) multiplexer_141 (
    .in0(multiplexer_109_out), .in1(multiplexer_125_out), .out(out_3[12]), .sel(in_1[4]));
  Multiplexer #(.enable("false")) multiplexer_142 (
    .in0(multiplexer_110_out), .in1(multiplexer_126_out), .out(out_3[13]), .sel(in_1[4]));
  Multiplexer #(.enable("false")) multiplexer_143 (
    .in0(multiplexer_111_out), .in1(multiplexer_127_out), .out(out_3[14]), .sel(in_1[4]));
  Multiplexer #(.enable("false")) multiplexer_144 (
    .in0(multiplexer_112_out), .in1(multiplexer_128_out), .out(out_3[15]), .sel(in_1[4]));
  Multiplexer #(.enable("false")) multiplexer_145 (
    .in0(multiplexer_113_out), .in1(1'b0), .out(out_3[16]), .sel(in_1[4]));
  Multiplexer #(.enable("false")) multiplexer_146 (
    .in0(multiplexer_114_out), .in1(1'b0), .out(out_3[17]), .sel(in_1[4]));
  Multiplexer #(.enable("false")) multiplexer_147 (
    .in0(multiplexer_115_out), .in1(1'b0), .out(out_3[18]), .sel(in_1[4]));
  Multiplexer #(.enable("false")) multiplexer_148 (
    .in0(multiplexer_116_out), .in1(1'b0), .out(out_3[19]), .sel(in_1[4]));
  Multiplexer #(.enable("false")) multiplexer_149 (
    .in0(multiplexer_117_out), .in1(1'b0), .out(out_3[20]), .sel(in_1[4]));
  Multiplexer #(.enable("false")) multiplexer_150 (
    .in0(multiplexer_118_out), .in1(1'b0), .out(out_3[21]), .sel(in_1[4]));
  Multiplexer #(.enable("false")) multiplexer_151 (
    .in0(multiplexer_119_out), .in1(1'b0), .out(out_3[22]), .sel(in_1[4]));
  Multiplexer #(.enable("false")) multiplexer_152 (
    .in0(multiplexer_120_out), .in1(1'b0), .out(out_3[23]), .sel(in_1[4]));
  Multiplexer #(.enable("false")) multiplexer_153 (
    .in0(multiplexer_121_out), .in1(1'b0), .out(out_3[24]), .sel(in_1[4]));
  Multiplexer #(.enable("false")) multiplexer_154 (
    .in0(multiplexer_122_out), .in1(1'b0), .out(out_3[25]), .sel(in_1[4]));
  Multiplexer #(.enable("false")) multiplexer_155 (
    .in0(multiplexer_123_out), .in1(1'b0), .out(out_3[26]), .sel(in_1[4]));
  Multiplexer #(.enable("false")) multiplexer_156 (
    .in0(multiplexer_124_out), .in1(1'b0), .out(out_3[27]), .sel(in_1[4]));
  Multiplexer #(.enable("false")) multiplexer_157 (
    .in0(multiplexer_125_out), .in1(1'b0), .out(out_3[28]), .sel(in_1[4]));
  Multiplexer #(.enable("false")) multiplexer_158 (
    .in0(multiplexer_126_out), .in1(1'b0), .out(out_3[29]), .sel(in_1[4]));
  Multiplexer #(.enable("false")) multiplexer_159 (
    .in0(multiplexer_127_out), .in1(1'b0), .out(out_3[30]), .sel(in_1[4]));
  Multiplexer #(.enable("false")) multiplexer_160 (
    .in0(multiplexer_128_out), .in1(1'b0), .out(out_3[31]), .sel(in_1[4]));

  // Notes on the sheet:
  //   5
  //   10
  //   15
  //   20
  //   25
  //   30
  //   5
  //   10
  //   15
  //   20
  //   25
  //   30
  //   5
  //   10
  //   15
  //   20
  //   25
  //   30
  //   5
  //   5
  //   10
  //   10
  //   15
  //   15
  //   20
  //   20
  //   25
  //   25
  //   30
  //   30
  //   5
  //   10
  //   15
  //   20
  //   25
  //   30
endmodule

module SRA (
  input  [4:0] in_1,
  input  [31:0] in_2,
  output [31:0] out_3
);

  wire multiplexer_1_out, multiplexer_2_out, multiplexer_3_out, multiplexer_4_out, multiplexer_5_out,
       multiplexer_6_out, multiplexer_7_out, multiplexer_8_out, multiplexer_9_out, multiplexer_10_out,
       multiplexer_11_out, multiplexer_12_out, multiplexer_13_out, multiplexer_14_out, multiplexer_15_out,
       multiplexer_16_out, multiplexer_17_out, multiplexer_18_out, multiplexer_19_out, multiplexer_20_out,
       multiplexer_21_out, multiplexer_22_out, multiplexer_23_out, multiplexer_24_out, multiplexer_25_out,
       multiplexer_26_out, multiplexer_27_out, multiplexer_28_out, multiplexer_29_out, multiplexer_30_out,
       multiplexer_31_out, multiplexer_32_out, multiplexer_33_out, multiplexer_34_out, multiplexer_35_out,
       multiplexer_36_out, multiplexer_37_out, multiplexer_38_out, multiplexer_39_out, multiplexer_40_out,
       multiplexer_41_out, multiplexer_42_out, multiplexer_43_out, multiplexer_44_out, multiplexer_45_out,
       multiplexer_46_out, multiplexer_47_out, multiplexer_48_out, multiplexer_49_out, multiplexer_50_out,
       multiplexer_51_out, multiplexer_52_out, multiplexer_53_out, multiplexer_54_out, multiplexer_55_out,
       multiplexer_56_out, multiplexer_57_out, multiplexer_58_out, multiplexer_59_out, multiplexer_60_out,
       multiplexer_61_out, multiplexer_62_out, multiplexer_63_out, multiplexer_64_out, multiplexer_65_out,
       multiplexer_66_out, multiplexer_67_out, multiplexer_68_out, multiplexer_69_out, multiplexer_70_out,
       multiplexer_71_out, multiplexer_72_out, multiplexer_73_out, multiplexer_74_out, multiplexer_75_out,
       multiplexer_76_out, multiplexer_77_out, multiplexer_78_out, multiplexer_79_out, multiplexer_80_out,
       multiplexer_81_out, multiplexer_82_out, multiplexer_83_out, multiplexer_84_out, multiplexer_85_out,
       multiplexer_86_out, multiplexer_87_out, multiplexer_88_out, multiplexer_89_out, multiplexer_90_out,
       multiplexer_91_out, multiplexer_92_out, multiplexer_93_out, multiplexer_94_out, multiplexer_95_out,
       multiplexer_96_out, multiplexer_97_out, multiplexer_98_out, multiplexer_99_out, multiplexer_100_out,
       multiplexer_101_out, multiplexer_102_out, multiplexer_103_out, multiplexer_104_out,
       multiplexer_105_out, multiplexer_106_out, multiplexer_107_out, multiplexer_108_out,
       multiplexer_109_out, multiplexer_110_out, multiplexer_111_out, multiplexer_112_out,
       multiplexer_113_out, multiplexer_114_out, multiplexer_115_out, multiplexer_116_out,
       multiplexer_117_out, multiplexer_118_out, multiplexer_119_out, multiplexer_120_out,
       multiplexer_121_out, multiplexer_122_out, multiplexer_123_out, multiplexer_124_out,
       multiplexer_125_out, multiplexer_126_out, multiplexer_127_out, multiplexer_128_out;

  Multiplexer #(.enable("false")) multiplexer_1 (.in0(in_2[0]), .in1(in_2[1]), .out(multiplexer_1_out), .sel(in_1[0]));
  Multiplexer #(.enable("false")) multiplexer_2 (.in0(in_2[1]), .in1(in_2[2]), .out(multiplexer_2_out), .sel(in_1[0]));
  Multiplexer #(.enable("false")) multiplexer_3 (.in0(in_2[2]), .in1(in_2[3]), .out(multiplexer_3_out), .sel(in_1[0]));
  Multiplexer #(.enable("false")) multiplexer_4 (.in0(in_2[3]), .in1(in_2[4]), .out(multiplexer_4_out), .sel(in_1[0]));
  Multiplexer #(.enable("false")) multiplexer_5 (.in0(in_2[4]), .in1(in_2[5]), .out(multiplexer_5_out), .sel(in_1[0]));
  Multiplexer #(.enable("false")) multiplexer_6 (.in0(in_2[5]), .in1(in_2[6]), .out(multiplexer_6_out), .sel(in_1[0]));
  Multiplexer #(.enable("false")) multiplexer_7 (.in0(in_2[6]), .in1(in_2[7]), .out(multiplexer_7_out), .sel(in_1[0]));
  Multiplexer #(.enable("false")) multiplexer_8 (.in0(in_2[7]), .in1(in_2[8]), .out(multiplexer_8_out), .sel(in_1[0]));
  Multiplexer #(.enable("false")) multiplexer_9 (.in0(in_2[8]), .in1(in_2[9]), .out(multiplexer_9_out), .sel(in_1[0]));
  Multiplexer #(.enable("false")) multiplexer_10 (
    .in0(in_2[9]), .in1(in_2[10]), .out(multiplexer_10_out), .sel(in_1[0]));
  Multiplexer #(.enable("false")) multiplexer_11 (
    .in0(in_2[10]), .in1(in_2[11]), .out(multiplexer_11_out), .sel(in_1[0]));
  Multiplexer #(.enable("false")) multiplexer_12 (
    .in0(in_2[11]), .in1(in_2[12]), .out(multiplexer_12_out), .sel(in_1[0]));
  Multiplexer #(.enable("false")) multiplexer_13 (
    .in0(in_2[12]), .in1(in_2[13]), .out(multiplexer_13_out), .sel(in_1[0]));
  Multiplexer #(.enable("false")) multiplexer_14 (
    .in0(in_2[13]), .in1(in_2[14]), .out(multiplexer_14_out), .sel(in_1[0]));
  Multiplexer #(.enable("false")) multiplexer_15 (
    .in0(in_2[14]), .in1(in_2[15]), .out(multiplexer_15_out), .sel(in_1[0]));
  Multiplexer #(.enable("false")) multiplexer_16 (
    .in0(in_2[15]), .in1(in_2[16]), .out(multiplexer_16_out), .sel(in_1[0]));
  Multiplexer #(.enable("false")) multiplexer_17 (
    .in0(in_2[16]), .in1(in_2[17]), .out(multiplexer_17_out), .sel(in_1[0]));
  Multiplexer #(.enable("false")) multiplexer_18 (
    .in0(in_2[17]), .in1(in_2[18]), .out(multiplexer_18_out), .sel(in_1[0]));
  Multiplexer #(.enable("false")) multiplexer_19 (
    .in0(in_2[18]), .in1(in_2[19]), .out(multiplexer_19_out), .sel(in_1[0]));
  Multiplexer #(.enable("false")) multiplexer_20 (
    .in0(in_2[19]), .in1(in_2[20]), .out(multiplexer_20_out), .sel(in_1[0]));
  Multiplexer #(.enable("false")) multiplexer_21 (
    .in0(in_2[20]), .in1(in_2[21]), .out(multiplexer_21_out), .sel(in_1[0]));
  Multiplexer #(.enable("false")) multiplexer_22 (
    .in0(in_2[21]), .in1(in_2[22]), .out(multiplexer_22_out), .sel(in_1[0]));
  Multiplexer #(.enable("false")) multiplexer_23 (
    .in0(in_2[22]), .in1(in_2[23]), .out(multiplexer_23_out), .sel(in_1[0]));
  Multiplexer #(.enable("false")) multiplexer_24 (
    .in0(in_2[23]), .in1(in_2[24]), .out(multiplexer_24_out), .sel(in_1[0]));
  Multiplexer #(.enable("false")) multiplexer_25 (
    .in0(in_2[24]), .in1(in_2[25]), .out(multiplexer_25_out), .sel(in_1[0]));
  Multiplexer #(.enable("false")) multiplexer_26 (
    .in0(in_2[25]), .in1(in_2[26]), .out(multiplexer_26_out), .sel(in_1[0]));
  Multiplexer #(.enable("false")) multiplexer_27 (
    .in0(in_2[26]), .in1(in_2[27]), .out(multiplexer_27_out), .sel(in_1[0]));
  Multiplexer #(.enable("false")) multiplexer_28 (
    .in0(in_2[27]), .in1(in_2[28]), .out(multiplexer_28_out), .sel(in_1[0]));
  Multiplexer #(.enable("false")) multiplexer_29 (
    .in0(in_2[28]), .in1(in_2[29]), .out(multiplexer_29_out), .sel(in_1[0]));
  Multiplexer #(.enable("false")) multiplexer_30 (
    .in0(in_2[29]), .in1(in_2[30]), .out(multiplexer_30_out), .sel(in_1[0]));
  Multiplexer #(.enable("false")) multiplexer_31 (
    .in0(in_2[30]), .in1(in_2[31]), .out(multiplexer_31_out), .sel(in_1[0]));
  Multiplexer #(.enable("false")) multiplexer_32 (
    .in0(in_2[31]), .in1(in_2[31]), .out(multiplexer_32_out), .sel(in_1[0]));
  Multiplexer #(.enable("false")) multiplexer_33 (
    .in0(multiplexer_1_out), .in1(multiplexer_3_out), .out(multiplexer_33_out), .sel(in_1[1]));
  Multiplexer #(.enable("false")) multiplexer_34 (
    .in0(multiplexer_2_out), .in1(multiplexer_4_out), .out(multiplexer_34_out), .sel(in_1[1]));
  Multiplexer #(.enable("false")) multiplexer_35 (
    .in0(multiplexer_3_out), .in1(multiplexer_5_out), .out(multiplexer_35_out), .sel(in_1[1]));
  Multiplexer #(.enable("false")) multiplexer_36 (
    .in0(multiplexer_4_out), .in1(multiplexer_6_out), .out(multiplexer_36_out), .sel(in_1[1]));
  Multiplexer #(.enable("false")) multiplexer_37 (
    .in0(multiplexer_5_out), .in1(multiplexer_7_out), .out(multiplexer_37_out), .sel(in_1[1]));
  Multiplexer #(.enable("false")) multiplexer_38 (
    .in0(multiplexer_6_out), .in1(multiplexer_8_out), .out(multiplexer_38_out), .sel(in_1[1]));
  Multiplexer #(.enable("false")) multiplexer_39 (
    .in0(multiplexer_7_out), .in1(multiplexer_9_out), .out(multiplexer_39_out), .sel(in_1[1]));
  Multiplexer #(.enable("false")) multiplexer_40 (
    .in0(multiplexer_8_out), .in1(multiplexer_10_out), .out(multiplexer_40_out), .sel(in_1[1]));
  Multiplexer #(.enable("false")) multiplexer_41 (
    .in0(multiplexer_9_out), .in1(multiplexer_11_out), .out(multiplexer_41_out), .sel(in_1[1]));
  Multiplexer #(.enable("false")) multiplexer_42 (
    .in0(multiplexer_10_out), .in1(multiplexer_12_out), .out(multiplexer_42_out), .sel(in_1[1]));
  Multiplexer #(.enable("false")) multiplexer_43 (
    .in0(multiplexer_11_out), .in1(multiplexer_13_out), .out(multiplexer_43_out), .sel(in_1[1]));
  Multiplexer #(.enable("false")) multiplexer_44 (
    .in0(multiplexer_12_out), .in1(multiplexer_14_out), .out(multiplexer_44_out), .sel(in_1[1]));
  Multiplexer #(.enable("false")) multiplexer_45 (
    .in0(multiplexer_13_out), .in1(multiplexer_15_out), .out(multiplexer_45_out), .sel(in_1[1]));
  Multiplexer #(.enable("false")) multiplexer_46 (
    .in0(multiplexer_14_out), .in1(multiplexer_16_out), .out(multiplexer_46_out), .sel(in_1[1]));
  Multiplexer #(.enable("false")) multiplexer_47 (
    .in0(multiplexer_15_out), .in1(multiplexer_17_out), .out(multiplexer_47_out), .sel(in_1[1]));
  Multiplexer #(.enable("false")) multiplexer_48 (
    .in0(multiplexer_16_out), .in1(multiplexer_18_out), .out(multiplexer_48_out), .sel(in_1[1]));
  Multiplexer #(.enable("false")) multiplexer_49 (
    .in0(multiplexer_17_out), .in1(multiplexer_19_out), .out(multiplexer_49_out), .sel(in_1[1]));
  Multiplexer #(.enable("false")) multiplexer_50 (
    .in0(multiplexer_18_out), .in1(multiplexer_20_out), .out(multiplexer_50_out), .sel(in_1[1]));
  Multiplexer #(.enable("false")) multiplexer_51 (
    .in0(multiplexer_19_out), .in1(multiplexer_21_out), .out(multiplexer_51_out), .sel(in_1[1]));
  Multiplexer #(.enable("false")) multiplexer_52 (
    .in0(multiplexer_20_out), .in1(multiplexer_22_out), .out(multiplexer_52_out), .sel(in_1[1]));
  Multiplexer #(.enable("false")) multiplexer_53 (
    .in0(multiplexer_21_out), .in1(multiplexer_23_out), .out(multiplexer_53_out), .sel(in_1[1]));
  Multiplexer #(.enable("false")) multiplexer_54 (
    .in0(multiplexer_22_out), .in1(multiplexer_24_out), .out(multiplexer_54_out), .sel(in_1[1]));
  Multiplexer #(.enable("false")) multiplexer_55 (
    .in0(multiplexer_23_out), .in1(multiplexer_25_out), .out(multiplexer_55_out), .sel(in_1[1]));
  Multiplexer #(.enable("false")) multiplexer_56 (
    .in0(multiplexer_24_out), .in1(multiplexer_26_out), .out(multiplexer_56_out), .sel(in_1[1]));
  Multiplexer #(.enable("false")) multiplexer_57 (
    .in0(multiplexer_25_out), .in1(multiplexer_27_out), .out(multiplexer_57_out), .sel(in_1[1]));
  Multiplexer #(.enable("false")) multiplexer_58 (
    .in0(multiplexer_26_out), .in1(multiplexer_28_out), .out(multiplexer_58_out), .sel(in_1[1]));
  Multiplexer #(.enable("false")) multiplexer_59 (
    .in0(multiplexer_27_out), .in1(multiplexer_29_out), .out(multiplexer_59_out), .sel(in_1[1]));
  Multiplexer #(.enable("false")) multiplexer_60 (
    .in0(multiplexer_28_out), .in1(multiplexer_30_out), .out(multiplexer_60_out), .sel(in_1[1]));
  Multiplexer #(.enable("false")) multiplexer_61 (
    .in0(multiplexer_29_out), .in1(multiplexer_31_out), .out(multiplexer_61_out), .sel(in_1[1]));
  Multiplexer #(.enable("false")) multiplexer_62 (
    .in0(multiplexer_30_out), .in1(multiplexer_32_out), .out(multiplexer_62_out), .sel(in_1[1]));
  Multiplexer #(.enable("false")) multiplexer_63 (
    .in0(multiplexer_31_out), .in1(in_2[31]), .out(multiplexer_63_out), .sel(in_1[1]));
  Multiplexer #(.enable("false")) multiplexer_64 (
    .in0(multiplexer_32_out), .in1(in_2[31]), .out(multiplexer_64_out), .sel(in_1[1]));
  Multiplexer #(.enable("false")) multiplexer_65 (
    .in0(multiplexer_33_out), .in1(multiplexer_37_out), .out(multiplexer_65_out), .sel(in_1[2]));
  Multiplexer #(.enable("false")) multiplexer_66 (
    .in0(multiplexer_34_out), .in1(multiplexer_38_out), .out(multiplexer_66_out), .sel(in_1[2]));
  Multiplexer #(.enable("false")) multiplexer_67 (
    .in0(multiplexer_35_out), .in1(multiplexer_39_out), .out(multiplexer_67_out), .sel(in_1[2]));
  Multiplexer #(.enable("false")) multiplexer_68 (
    .in0(multiplexer_36_out), .in1(multiplexer_40_out), .out(multiplexer_68_out), .sel(in_1[2]));
  Multiplexer #(.enable("false")) multiplexer_69 (
    .in0(multiplexer_37_out), .in1(multiplexer_41_out), .out(multiplexer_69_out), .sel(in_1[2]));
  Multiplexer #(.enable("false")) multiplexer_70 (
    .in0(multiplexer_38_out), .in1(multiplexer_42_out), .out(multiplexer_70_out), .sel(in_1[2]));
  Multiplexer #(.enable("false")) multiplexer_71 (
    .in0(multiplexer_39_out), .in1(multiplexer_43_out), .out(multiplexer_71_out), .sel(in_1[2]));
  Multiplexer #(.enable("false")) multiplexer_72 (
    .in0(multiplexer_40_out), .in1(multiplexer_44_out), .out(multiplexer_72_out), .sel(in_1[2]));
  Multiplexer #(.enable("false")) multiplexer_73 (
    .in0(multiplexer_41_out), .in1(multiplexer_45_out), .out(multiplexer_73_out), .sel(in_1[2]));
  Multiplexer #(.enable("false")) multiplexer_74 (
    .in0(multiplexer_42_out), .in1(multiplexer_46_out), .out(multiplexer_74_out), .sel(in_1[2]));
  Multiplexer #(.enable("false")) multiplexer_75 (
    .in0(multiplexer_43_out), .in1(multiplexer_47_out), .out(multiplexer_75_out), .sel(in_1[2]));
  Multiplexer #(.enable("false")) multiplexer_76 (
    .in0(multiplexer_44_out), .in1(multiplexer_48_out), .out(multiplexer_76_out), .sel(in_1[2]));
  Multiplexer #(.enable("false")) multiplexer_77 (
    .in0(multiplexer_45_out), .in1(multiplexer_49_out), .out(multiplexer_77_out), .sel(in_1[2]));
  Multiplexer #(.enable("false")) multiplexer_78 (
    .in0(multiplexer_46_out), .in1(multiplexer_50_out), .out(multiplexer_78_out), .sel(in_1[2]));
  Multiplexer #(.enable("false")) multiplexer_79 (
    .in0(multiplexer_47_out), .in1(multiplexer_51_out), .out(multiplexer_79_out), .sel(in_1[2]));
  Multiplexer #(.enable("false")) multiplexer_80 (
    .in0(multiplexer_48_out), .in1(multiplexer_52_out), .out(multiplexer_80_out), .sel(in_1[2]));
  Multiplexer #(.enable("false")) multiplexer_81 (
    .in0(multiplexer_49_out), .in1(multiplexer_53_out), .out(multiplexer_81_out), .sel(in_1[2]));
  Multiplexer #(.enable("false")) multiplexer_82 (
    .in0(multiplexer_50_out), .in1(multiplexer_54_out), .out(multiplexer_82_out), .sel(in_1[2]));
  Multiplexer #(.enable("false")) multiplexer_83 (
    .in0(multiplexer_51_out), .in1(multiplexer_55_out), .out(multiplexer_83_out), .sel(in_1[2]));
  Multiplexer #(.enable("false")) multiplexer_84 (
    .in0(multiplexer_52_out), .in1(multiplexer_56_out), .out(multiplexer_84_out), .sel(in_1[2]));
  Multiplexer #(.enable("false")) multiplexer_85 (
    .in0(multiplexer_53_out), .in1(multiplexer_57_out), .out(multiplexer_85_out), .sel(in_1[2]));
  Multiplexer #(.enable("false")) multiplexer_86 (
    .in0(multiplexer_54_out), .in1(multiplexer_58_out), .out(multiplexer_86_out), .sel(in_1[2]));
  Multiplexer #(.enable("false")) multiplexer_87 (
    .in0(multiplexer_55_out), .in1(multiplexer_59_out), .out(multiplexer_87_out), .sel(in_1[2]));
  Multiplexer #(.enable("false")) multiplexer_88 (
    .in0(multiplexer_56_out), .in1(multiplexer_60_out), .out(multiplexer_88_out), .sel(in_1[2]));
  Multiplexer #(.enable("false")) multiplexer_89 (
    .in0(multiplexer_57_out), .in1(multiplexer_61_out), .out(multiplexer_89_out), .sel(in_1[2]));
  Multiplexer #(.enable("false")) multiplexer_90 (
    .in0(multiplexer_58_out), .in1(multiplexer_62_out), .out(multiplexer_90_out), .sel(in_1[2]));
  Multiplexer #(.enable("false")) multiplexer_91 (
    .in0(multiplexer_59_out), .in1(multiplexer_63_out), .out(multiplexer_91_out), .sel(in_1[2]));
  Multiplexer #(.enable("false")) multiplexer_92 (
    .in0(multiplexer_60_out), .in1(multiplexer_64_out), .out(multiplexer_92_out), .sel(in_1[2]));
  Multiplexer #(.enable("false")) multiplexer_93 (
    .in0(multiplexer_61_out), .in1(in_2[31]), .out(multiplexer_93_out), .sel(in_1[2]));
  Multiplexer #(.enable("false")) multiplexer_94 (
    .in0(multiplexer_62_out), .in1(in_2[31]), .out(multiplexer_94_out), .sel(in_1[2]));
  Multiplexer #(.enable("false")) multiplexer_95 (
    .in0(multiplexer_63_out), .in1(in_2[31]), .out(multiplexer_95_out), .sel(in_1[2]));
  Multiplexer #(.enable("false")) multiplexer_96 (
    .in0(multiplexer_64_out), .in1(in_2[31]), .out(multiplexer_96_out), .sel(in_1[2]));
  Multiplexer #(.enable("false")) multiplexer_97 (
    .in0(multiplexer_65_out), .in1(multiplexer_73_out), .out(multiplexer_97_out), .sel(in_1[3]));
  Multiplexer #(.enable("false")) multiplexer_98 (
    .in0(multiplexer_66_out), .in1(multiplexer_74_out), .out(multiplexer_98_out), .sel(in_1[3]));
  Multiplexer #(.enable("false")) multiplexer_99 (
    .in0(multiplexer_67_out), .in1(multiplexer_75_out), .out(multiplexer_99_out), .sel(in_1[3]));
  Multiplexer #(.enable("false")) multiplexer_100 (
    .in0(multiplexer_68_out), .in1(multiplexer_76_out), .out(multiplexer_100_out), .sel(in_1[3]));
  Multiplexer #(.enable("false")) multiplexer_101 (
    .in0(multiplexer_69_out), .in1(multiplexer_77_out), .out(multiplexer_101_out), .sel(in_1[3]));
  Multiplexer #(.enable("false")) multiplexer_102 (
    .in0(multiplexer_70_out), .in1(multiplexer_78_out), .out(multiplexer_102_out), .sel(in_1[3]));
  Multiplexer #(.enable("false")) multiplexer_103 (
    .in0(multiplexer_71_out), .in1(multiplexer_79_out), .out(multiplexer_103_out), .sel(in_1[3]));
  Multiplexer #(.enable("false")) multiplexer_104 (
    .in0(multiplexer_72_out), .in1(multiplexer_80_out), .out(multiplexer_104_out), .sel(in_1[3]));
  Multiplexer #(.enable("false")) multiplexer_105 (
    .in0(multiplexer_73_out), .in1(multiplexer_81_out), .out(multiplexer_105_out), .sel(in_1[3]));
  Multiplexer #(.enable("false")) multiplexer_106 (
    .in0(multiplexer_74_out), .in1(multiplexer_82_out), .out(multiplexer_106_out), .sel(in_1[3]));
  Multiplexer #(.enable("false")) multiplexer_107 (
    .in0(multiplexer_75_out), .in1(multiplexer_83_out), .out(multiplexer_107_out), .sel(in_1[3]));
  Multiplexer #(.enable("false")) multiplexer_108 (
    .in0(multiplexer_76_out), .in1(multiplexer_84_out), .out(multiplexer_108_out), .sel(in_1[3]));
  Multiplexer #(.enable("false")) multiplexer_109 (
    .in0(multiplexer_77_out), .in1(multiplexer_85_out), .out(multiplexer_109_out), .sel(in_1[3]));
  Multiplexer #(.enable("false")) multiplexer_110 (
    .in0(multiplexer_78_out), .in1(multiplexer_86_out), .out(multiplexer_110_out), .sel(in_1[3]));
  Multiplexer #(.enable("false")) multiplexer_111 (
    .in0(multiplexer_79_out), .in1(multiplexer_87_out), .out(multiplexer_111_out), .sel(in_1[3]));
  Multiplexer #(.enable("false")) multiplexer_112 (
    .in0(multiplexer_80_out), .in1(multiplexer_88_out), .out(multiplexer_112_out), .sel(in_1[3]));
  Multiplexer #(.enable("false")) multiplexer_113 (
    .in0(multiplexer_81_out), .in1(multiplexer_89_out), .out(multiplexer_113_out), .sel(in_1[3]));
  Multiplexer #(.enable("false")) multiplexer_114 (
    .in0(multiplexer_82_out), .in1(multiplexer_90_out), .out(multiplexer_114_out), .sel(in_1[3]));
  Multiplexer #(.enable("false")) multiplexer_115 (
    .in0(multiplexer_83_out), .in1(multiplexer_91_out), .out(multiplexer_115_out), .sel(in_1[3]));
  Multiplexer #(.enable("false")) multiplexer_116 (
    .in0(multiplexer_84_out), .in1(multiplexer_92_out), .out(multiplexer_116_out), .sel(in_1[3]));
  Multiplexer #(.enable("false")) multiplexer_117 (
    .in0(multiplexer_85_out), .in1(multiplexer_93_out), .out(multiplexer_117_out), .sel(in_1[3]));
  Multiplexer #(.enable("false")) multiplexer_118 (
    .in0(multiplexer_86_out), .in1(multiplexer_94_out), .out(multiplexer_118_out), .sel(in_1[3]));
  Multiplexer #(.enable("false")) multiplexer_119 (
    .in0(multiplexer_87_out), .in1(multiplexer_95_out), .out(multiplexer_119_out), .sel(in_1[3]));
  Multiplexer #(.enable("false")) multiplexer_120 (
    .in0(multiplexer_88_out), .in1(multiplexer_96_out), .out(multiplexer_120_out), .sel(in_1[3]));
  Multiplexer #(.enable("false")) multiplexer_121 (
    .in0(multiplexer_89_out), .in1(in_2[31]), .out(multiplexer_121_out), .sel(in_1[3]));
  Multiplexer #(.enable("false")) multiplexer_122 (
    .in0(multiplexer_90_out), .in1(in_2[31]), .out(multiplexer_122_out), .sel(in_1[3]));
  Multiplexer #(.enable("false")) multiplexer_123 (
    .in0(multiplexer_91_out), .in1(in_2[31]), .out(multiplexer_123_out), .sel(in_1[3]));
  Multiplexer #(.enable("false")) multiplexer_124 (
    .in0(multiplexer_92_out), .in1(in_2[31]), .out(multiplexer_124_out), .sel(in_1[3]));
  Multiplexer #(.enable("false")) multiplexer_125 (
    .in0(multiplexer_93_out), .in1(in_2[31]), .out(multiplexer_125_out), .sel(in_1[3]));
  Multiplexer #(.enable("false")) multiplexer_126 (
    .in0(multiplexer_94_out), .in1(in_2[31]), .out(multiplexer_126_out), .sel(in_1[3]));
  Multiplexer #(.enable("false")) multiplexer_127 (
    .in0(multiplexer_95_out), .in1(in_2[31]), .out(multiplexer_127_out), .sel(in_1[3]));
  Multiplexer #(.enable("false")) multiplexer_128 (
    .in0(multiplexer_96_out), .in1(in_2[31]), .out(multiplexer_128_out), .sel(in_1[3]));
  Multiplexer #(.enable("false")) multiplexer_129 (
    .in0(multiplexer_97_out), .in1(multiplexer_113_out), .out(out_3[0]), .sel(in_1[4]));
  Multiplexer #(.enable("false")) multiplexer_130 (
    .in0(multiplexer_98_out), .in1(multiplexer_114_out), .out(out_3[1]), .sel(in_1[4]));
  Multiplexer #(.enable("false")) multiplexer_131 (
    .in0(multiplexer_99_out), .in1(multiplexer_115_out), .out(out_3[2]), .sel(in_1[4]));
  Multiplexer #(.enable("false")) multiplexer_132 (
    .in0(multiplexer_100_out), .in1(multiplexer_116_out), .out(out_3[3]), .sel(in_1[4]));
  Multiplexer #(.enable("false")) multiplexer_133 (
    .in0(multiplexer_101_out), .in1(multiplexer_117_out), .out(out_3[4]), .sel(in_1[4]));
  Multiplexer #(.enable("false")) multiplexer_134 (
    .in0(multiplexer_102_out), .in1(multiplexer_118_out), .out(out_3[5]), .sel(in_1[4]));
  Multiplexer #(.enable("false")) multiplexer_135 (
    .in0(multiplexer_103_out), .in1(multiplexer_119_out), .out(out_3[6]), .sel(in_1[4]));
  Multiplexer #(.enable("false")) multiplexer_136 (
    .in0(multiplexer_104_out), .in1(multiplexer_120_out), .out(out_3[7]), .sel(in_1[4]));
  Multiplexer #(.enable("false")) multiplexer_137 (
    .in0(multiplexer_105_out), .in1(multiplexer_121_out), .out(out_3[8]), .sel(in_1[4]));
  Multiplexer #(.enable("false")) multiplexer_138 (
    .in0(multiplexer_106_out), .in1(multiplexer_122_out), .out(out_3[9]), .sel(in_1[4]));
  Multiplexer #(.enable("false")) multiplexer_139 (
    .in0(multiplexer_107_out), .in1(multiplexer_123_out), .out(out_3[10]), .sel(in_1[4]));
  Multiplexer #(.enable("false")) multiplexer_140 (
    .in0(multiplexer_108_out), .in1(multiplexer_124_out), .out(out_3[11]), .sel(in_1[4]));
  Multiplexer #(.enable("false")) multiplexer_141 (
    .in0(multiplexer_109_out), .in1(multiplexer_125_out), .out(out_3[12]), .sel(in_1[4]));
  Multiplexer #(.enable("false")) multiplexer_142 (
    .in0(multiplexer_110_out), .in1(multiplexer_126_out), .out(out_3[13]), .sel(in_1[4]));
  Multiplexer #(.enable("false")) multiplexer_143 (
    .in0(multiplexer_111_out), .in1(multiplexer_127_out), .out(out_3[14]), .sel(in_1[4]));
  Multiplexer #(.enable("false")) multiplexer_144 (
    .in0(multiplexer_112_out), .in1(multiplexer_128_out), .out(out_3[15]), .sel(in_1[4]));
  Multiplexer #(.enable("false")) multiplexer_145 (
    .in0(multiplexer_113_out), .in1(in_2[31]), .out(out_3[16]), .sel(in_1[4]));
  Multiplexer #(.enable("false")) multiplexer_146 (
    .in0(multiplexer_114_out), .in1(in_2[31]), .out(out_3[17]), .sel(in_1[4]));
  Multiplexer #(.enable("false")) multiplexer_147 (
    .in0(multiplexer_115_out), .in1(in_2[31]), .out(out_3[18]), .sel(in_1[4]));
  Multiplexer #(.enable("false")) multiplexer_148 (
    .in0(multiplexer_116_out), .in1(in_2[31]), .out(out_3[19]), .sel(in_1[4]));
  Multiplexer #(.enable("false")) multiplexer_149 (
    .in0(multiplexer_117_out), .in1(in_2[31]), .out(out_3[20]), .sel(in_1[4]));
  Multiplexer #(.enable("false")) multiplexer_150 (
    .in0(multiplexer_118_out), .in1(in_2[31]), .out(out_3[21]), .sel(in_1[4]));
  Multiplexer #(.enable("false")) multiplexer_151 (
    .in0(multiplexer_119_out), .in1(in_2[31]), .out(out_3[22]), .sel(in_1[4]));
  Multiplexer #(.enable("false")) multiplexer_152 (
    .in0(multiplexer_120_out), .in1(in_2[31]), .out(out_3[23]), .sel(in_1[4]));
  Multiplexer #(.enable("false")) multiplexer_153 (
    .in0(multiplexer_121_out), .in1(in_2[31]), .out(out_3[24]), .sel(in_1[4]));
  Multiplexer #(.enable("false")) multiplexer_154 (
    .in0(multiplexer_122_out), .in1(in_2[31]), .out(out_3[25]), .sel(in_1[4]));
  Multiplexer #(.enable("false")) multiplexer_155 (
    .in0(multiplexer_123_out), .in1(in_2[31]), .out(out_3[26]), .sel(in_1[4]));
  Multiplexer #(.enable("false")) multiplexer_156 (
    .in0(multiplexer_124_out), .in1(in_2[31]), .out(out_3[27]), .sel(in_1[4]));
  Multiplexer #(.enable("false")) multiplexer_157 (
    .in0(multiplexer_125_out), .in1(in_2[31]), .out(out_3[28]), .sel(in_1[4]));
  Multiplexer #(.enable("false")) multiplexer_158 (
    .in0(multiplexer_126_out), .in1(in_2[31]), .out(out_3[29]), .sel(in_1[4]));
  Multiplexer #(.enable("false")) multiplexer_159 (
    .in0(multiplexer_127_out), .in1(in_2[31]), .out(out_3[30]), .sel(in_1[4]));
  Multiplexer #(.enable("false")) multiplexer_160 (
    .in0(multiplexer_128_out), .in1(in_2[31]), .out(out_3[31]), .sel(in_1[4]));

  // Notes on the sheet:
  //   5
  //   10
  //   15
  //   20
  //   25
  //   30
  //   5
  //   10
  //   15
  //   20
  //   25
  //   30
  //   5
  //   10
  //   15
  //   20
  //   25
  //   30
  //   5
  //   5
  //   10
  //   10
  //   15
  //   15
  //   20
  //   20
  //   25
  //   25
  //   30
  //   30
  //   5
  //   10
  //   15
  //   20
  //   25
  //   30
endmodule

module registrador (
  input  [31:0] in_1,
  input  in_2,
  output [31:0] out_3
);

  D_Flip_Flop d_ff_1 (.clk(in_2), .D(in_1[23]), .Q(out_3[23]));  // open: Qn, preset, en, reset
  D_Flip_Flop d_ff_2 (.clk(in_2), .D(in_1[0]), .Q(out_3[0]));  // open: Qn, preset, en, reset
  D_Flip_Flop d_ff_3 (.clk(in_2), .D(in_1[15]), .Q(out_3[15]));  // open: Qn, preset, en, reset
  D_Flip_Flop d_ff_4 (.clk(in_2), .D(in_1[31]), .Q(out_3[31]));  // open: Qn, preset, en, reset
  D_Flip_Flop d_ff_5 (.clk(in_2), .D(in_1[1]), .Q(out_3[1]));  // open: Qn, preset, en, reset
  D_Flip_Flop d_ff_6 (.clk(in_2), .D(in_1[14]), .Q(out_3[14]));  // open: Qn, preset, en, reset
  D_Flip_Flop d_ff_7 (.clk(in_2), .D(in_1[22]), .Q(out_3[22]));  // open: Qn, preset, en, reset
  D_Flip_Flop d_ff_8 (.clk(in_2), .D(in_1[30]), .Q(out_3[30]));  // open: Qn, preset, en, reset
  D_Flip_Flop d_ff_9 (.clk(in_2), .D(in_1[2]), .Q(out_3[2]));  // open: Qn, preset, en, reset
  D_Flip_Flop d_ff_10 (.clk(in_2), .D(in_1[13]), .Q(out_3[13]));  // open: Qn, preset, en, reset
  D_Flip_Flop d_ff_11 (.clk(in_2), .D(in_1[21]), .Q(out_3[21]));  // open: Qn, preset, en, reset
  D_Flip_Flop d_ff_12 (.clk(in_2), .D(in_1[29]), .Q(out_3[29]));  // open: Qn, preset, en, reset
  D_Flip_Flop d_ff_13 (.clk(in_2), .D(in_1[12]), .Q(out_3[12]));  // open: Qn, preset, en, reset
  D_Flip_Flop d_ff_14 (.clk(in_2), .D(in_1[20]), .Q(out_3[20]));  // open: Qn, preset, en, reset
  D_Flip_Flop d_ff_15 (.clk(in_2), .D(in_1[28]), .Q(out_3[28]));  // open: Qn, preset, en, reset
  D_Flip_Flop d_ff_16 (.clk(in_2), .D(in_1[3]), .Q(out_3[3]));  // open: Qn, preset, en, reset
  D_Flip_Flop d_ff_17 (.clk(in_2), .D(in_1[4]), .Q(out_3[4]));  // open: Qn, preset, en, reset
  D_Flip_Flop d_ff_18 (.clk(in_2), .D(in_1[11]), .Q(out_3[11]));  // open: Qn, preset, en, reset
  D_Flip_Flop d_ff_19 (.clk(in_2), .D(in_1[19]), .Q(out_3[19]));  // open: Qn, preset, en, reset
  D_Flip_Flop d_ff_20 (.clk(in_2), .D(in_1[27]), .Q(out_3[27]));  // open: Qn, preset, en, reset
  D_Flip_Flop d_ff_21 (.clk(in_2), .D(in_1[18]), .Q(out_3[18]));  // open: Qn, preset, en, reset
  D_Flip_Flop d_ff_22 (.clk(in_2), .D(in_1[5]), .Q(out_3[5]));  // open: Qn, preset, en, reset
  D_Flip_Flop d_ff_23 (.clk(in_2), .D(in_1[10]), .Q(out_3[10]));  // open: Qn, preset, en, reset
  D_Flip_Flop d_ff_24 (.clk(in_2), .D(in_1[26]), .Q(out_3[26]));  // open: Qn, preset, en, reset
  D_Flip_Flop d_ff_25 (.clk(in_2), .D(in_1[6]), .Q(out_3[6]));  // open: Qn, preset, en, reset
  D_Flip_Flop d_ff_26 (.clk(in_2), .D(in_1[9]), .Q(out_3[9]));  // open: Qn, preset, en, reset
  D_Flip_Flop d_ff_27 (.clk(in_2), .D(in_1[17]), .Q(out_3[17]));  // open: Qn, preset, en, reset
  D_Flip_Flop d_ff_28 (.clk(in_2), .D(in_1[25]), .Q(out_3[25]));  // open: Qn, preset, en, reset
  D_Flip_Flop d_ff_29 (.clk(in_2), .D(in_1[7]), .Q(out_3[7]));  // open: Qn, preset, en, reset
  D_Flip_Flop d_ff_30 (.clk(in_2), .D(in_1[8]), .Q(out_3[8]));  // open: Qn, preset, en, reset
  D_Flip_Flop d_ff_31 (.clk(in_2), .D(in_1[16]), .Q(out_3[16]));  // open: Qn, preset, en, reset
  D_Flip_Flop d_ff_32 (.clk(in_2), .D(in_1[24]), .Q(out_3[24]));  // open: Qn, preset, en, reset
endmodule
module banco_de_registradores (
  input  [4:0] Oper_A,
  input  [31:0] in_2,
  input  Clock,
  input  [4:0] in_4,
  input  [4:0] in_5,
  output [31:0] out_6,
  output [31:0] out_7
);

  wire clock_1_out;
  wire [31:0] demultiplexer_1_out0, demultiplexer_1_out1, demultiplexer_1_out2, demultiplexer_1_out3,
       demultiplexer_1_out4, demultiplexer_1_out5, demultiplexer_1_out6, demultiplexer_1_out7,
       demultiplexer_1_out8, demultiplexer_1_out9, demultiplexer_1_out10, demultiplexer_1_out11,
       demultiplexer_1_out12, demultiplexer_1_out13, demultiplexer_1_out14, demultiplexer_1_out15,
       demultiplexer_1_out16, demultiplexer_1_out17, demultiplexer_1_out18, demultiplexer_1_out19,
       demultiplexer_1_out20, demultiplexer_1_out21, demultiplexer_1_out22, demultiplexer_1_out23,
       demultiplexer_1_out24, demultiplexer_1_out25, demultiplexer_1_out26, demultiplexer_1_out27,
       demultiplexer_1_out28, demultiplexer_1_out29, demultiplexer_1_out30, demultiplexer_1_out31,
       registrador_1_out_3, registrador_2_out_3, registrador_3_out_3, registrador_4_out_3,
       registrador_5_out_3, registrador_6_out_3, registrador_7_out_3, registrador_8_out_3,
       registrador_9_out_3, registrador_10_out_3, registrador_11_out_3, registrador_12_out_3,
       registrador_13_out_3, registrador_14_out_3, registrador_15_out_3, registrador_16_out_3,
       registrador_17_out_3, registrador_18_out_3, registrador_19_out_3, registrador_20_out_3,
       registrador_21_out_3, registrador_22_out_3, registrador_23_out_3, registrador_24_out_3,
       registrador_25_out_3, registrador_26_out_3, registrador_27_out_3, registrador_28_out_3,
       registrador_29_out_3, registrador_30_out_3, registrador_31_out_3, registrador_32_out_3;

  Clock clock_1 (.out(clock_1_out));
  Demultiplexer #(.select(5), .width(32), .enable("false")) demultiplexer_1 (
    .out0(demultiplexer_1_out0), .out1(demultiplexer_1_out1), .out2(demultiplexer_1_out2),
    .out3(demultiplexer_1_out3), .out4(demultiplexer_1_out4), .out5(demultiplexer_1_out5),
    .out6(demultiplexer_1_out6), .out7(demultiplexer_1_out7), .out8(demultiplexer_1_out8),
    .out9(demultiplexer_1_out9), .out10(demultiplexer_1_out10), .out11(demultiplexer_1_out11),
    .out12(demultiplexer_1_out12), .out13(demultiplexer_1_out13), .out14(demultiplexer_1_out14),
    .out15(demultiplexer_1_out15), .out16(demultiplexer_1_out16), .out17(demultiplexer_1_out17),
    .out18(demultiplexer_1_out18), .out19(demultiplexer_1_out19), .out20(demultiplexer_1_out20),
    .out21(demultiplexer_1_out21), .out22(demultiplexer_1_out22), .out23(demultiplexer_1_out23),
    .out24(demultiplexer_1_out24), .out25(demultiplexer_1_out25), .out26(demultiplexer_1_out26),
    .out27(demultiplexer_1_out27), .out28(demultiplexer_1_out28), .out29(demultiplexer_1_out29),
    .out30(demultiplexer_1_out30), .out31(demultiplexer_1_out31), .in(in_2), .sel(in_4));
  registrador registrador_1 (.in_1(demultiplexer_1_out7), .in_2(clock_1_out), .out_3(registrador_1_out_3));
  registrador registrador_2 (.in_1(demultiplexer_1_out15), .in_2(clock_1_out), .out_3(registrador_2_out_3));
  registrador registrador_3 (.in_1(demultiplexer_1_out23), .in_2(clock_1_out), .out_3(registrador_3_out_3));
  registrador registrador_4 (.in_1(demultiplexer_1_out31), .in_2(clock_1_out), .out_3(registrador_4_out_3));
  registrador registrador_5 (.in_1(demultiplexer_1_out6), .in_2(clock_1_out), .out_3(registrador_5_out_3));
  registrador registrador_6 (.in_1(demultiplexer_1_out14), .in_2(clock_1_out), .out_3(registrador_6_out_3));
  registrador registrador_7 (.in_1(demultiplexer_1_out22), .in_2(clock_1_out), .out_3(registrador_7_out_3));
  registrador registrador_8 (.in_1(demultiplexer_1_out30), .in_2(clock_1_out), .out_3(registrador_8_out_3));
  registrador registrador_9 (.in_1(demultiplexer_1_out5), .in_2(clock_1_out), .out_3(registrador_9_out_3));
  registrador registrador_10 (.in_1(demultiplexer_1_out13), .in_2(clock_1_out), .out_3(registrador_10_out_3));
  registrador registrador_11 (.in_1(demultiplexer_1_out21), .in_2(clock_1_out), .out_3(registrador_11_out_3));
  registrador registrador_12 (.in_1(demultiplexer_1_out29), .in_2(clock_1_out), .out_3(registrador_12_out_3));
  registrador registrador_13 (.in_1(demultiplexer_1_out4), .in_2(clock_1_out), .out_3(registrador_13_out_3));
  registrador registrador_14 (.in_1(demultiplexer_1_out12), .in_2(clock_1_out), .out_3(registrador_14_out_3));
  registrador registrador_15 (.in_1(demultiplexer_1_out20), .in_2(clock_1_out), .out_3(registrador_15_out_3));
  registrador registrador_16 (.in_1(demultiplexer_1_out28), .in_2(clock_1_out), .out_3(registrador_16_out_3));
  registrador registrador_17 (.in_1(demultiplexer_1_out3), .in_2(clock_1_out), .out_3(registrador_17_out_3));
  registrador registrador_18 (.in_1(demultiplexer_1_out11), .in_2(clock_1_out), .out_3(registrador_18_out_3));
  registrador registrador_19 (.in_1(demultiplexer_1_out19), .in_2(clock_1_out), .out_3(registrador_19_out_3));
  registrador registrador_20 (.in_1(demultiplexer_1_out27), .in_2(clock_1_out), .out_3(registrador_20_out_3));
  registrador registrador_21 (.in_1(demultiplexer_1_out2), .in_2(clock_1_out), .out_3(registrador_21_out_3));
  registrador registrador_22 (.in_1(demultiplexer_1_out10), .in_2(clock_1_out), .out_3(registrador_22_out_3));
  registrador registrador_23 (.in_1(demultiplexer_1_out18), .in_2(clock_1_out), .out_3(registrador_23_out_3));
  registrador registrador_24 (.in_1(demultiplexer_1_out26), .in_2(clock_1_out), .out_3(registrador_24_out_3));
  registrador registrador_25 (.in_1(demultiplexer_1_out1), .in_2(clock_1_out), .out_3(registrador_25_out_3));
  registrador registrador_26 (.in_1(demultiplexer_1_out9), .in_2(clock_1_out), .out_3(registrador_26_out_3));
  registrador registrador_27 (.in_1(demultiplexer_1_out17), .in_2(clock_1_out), .out_3(registrador_27_out_3));
  registrador registrador_28 (.in_1(demultiplexer_1_out25), .in_2(clock_1_out), .out_3(registrador_28_out_3));
  registrador registrador_29 (.in_1(demultiplexer_1_out0), .in_2(clock_1_out), .out_3(registrador_29_out_3));
  registrador registrador_30 (.in_1(demultiplexer_1_out8), .in_2(clock_1_out), .out_3(registrador_30_out_3));
  registrador registrador_31 (.in_1(demultiplexer_1_out16), .in_2(clock_1_out), .out_3(registrador_31_out_3));
  registrador registrador_32 (.in_1(demultiplexer_1_out24), .in_2(clock_1_out), .out_3(registrador_32_out_3));
  Multiplexer #(.select(5), .width(32), .enable("false")) multiplexer_1 (
    .in0(registrador_29_out_3), .in1(registrador_25_out_3), .in2(registrador_21_out_3),
    .in3(registrador_17_out_3), .in4(registrador_13_out_3), .in5(registrador_9_out_3),
    .in6(registrador_5_out_3), .in7(registrador_1_out_3), .in8(registrador_30_out_3),
    .in9(registrador_26_out_3), .in10(registrador_22_out_3), .in11(registrador_18_out_3),
    .in12(registrador_14_out_3), .in13(registrador_10_out_3), .in14(registrador_6_out_3),
    .in15(registrador_2_out_3), .in16(registrador_31_out_3), .in17(registrador_27_out_3),
    .in18(registrador_23_out_3), .in19(registrador_19_out_3), .in20(registrador_15_out_3),
    .in21(registrador_11_out_3), .in22(registrador_7_out_3), .in23(registrador_3_out_3),
    .in24(registrador_32_out_3), .in25(registrador_28_out_3), .in26(registrador_24_out_3),
    .in27(registrador_20_out_3), .in28(registrador_16_out_3), .in29(registrador_12_out_3),
    .in30(registrador_8_out_3), .in31(registrador_4_out_3), .out(out_7), .sel(in_5));
  Multiplexer #(.select(5), .width(32), .enable("false")) multiplexer_2 (
    .in0(registrador_29_out_3), .in1(registrador_25_out_3), .in2(registrador_21_out_3),
    .in3(registrador_17_out_3), .in4(registrador_13_out_3), .in5(registrador_9_out_3),
    .in6(registrador_5_out_3), .in7(registrador_1_out_3), .in8(registrador_30_out_3),
    .in9(registrador_26_out_3), .in10(registrador_22_out_3), .in11(registrador_18_out_3),
    .in12(registrador_14_out_3), .in13(registrador_10_out_3), .in14(registrador_6_out_3),
    .in15(registrador_2_out_3), .in16(registrador_31_out_3), .in17(registrador_27_out_3),
    .in18(registrador_23_out_3), .in19(registrador_19_out_3), .in20(registrador_15_out_3),
    .in21(registrador_11_out_3), .in22(registrador_7_out_3), .in23(registrador_3_out_3),
    .in24(registrador_32_out_3), .in25(registrador_28_out_3), .in26(registrador_24_out_3),
    .in27(registrador_20_out_3), .in28(registrador_16_out_3), .in29(registrador_12_out_3),
    .in30(registrador_8_out_3), .in31(registrador_4_out_3), .out(out_6), .sel(Oper_A));

  // Notes on the sheet:
  //   Entrada
  //   Oper Demux
  //   Saida A
  //   Saida B
  //   Oper B
endmodule

module banco_de_registradores_2 (
  input  [4:0] Oper_A,
  input  [31:0] in_2,
  input  Clock,
  input  [4:0] in_4,
  input  [4:0] in_5,
  output [31:0] out_6,
  output [31:0] out_7
);

  wire demultiplexer_1_out0, demultiplexer_1_out1, demultiplexer_1_out2, demultiplexer_1_out3,
       demultiplexer_1_out4, demultiplexer_1_out5, demultiplexer_1_out6, demultiplexer_1_out7,
       demultiplexer_1_out8, demultiplexer_1_out9, demultiplexer_1_out10, demultiplexer_1_out11,
       demultiplexer_1_out12, demultiplexer_1_out13, demultiplexer_1_out14, demultiplexer_1_out15,
       demultiplexer_1_out16, demultiplexer_1_out17, demultiplexer_1_out18, demultiplexer_1_out19,
       demultiplexer_1_out20, demultiplexer_1_out21, demultiplexer_1_out22, demultiplexer_1_out23,
       demultiplexer_1_out24, demultiplexer_1_out25, demultiplexer_1_out26, demultiplexer_1_out27,
       demultiplexer_1_out28, demultiplexer_1_out29, demultiplexer_1_out30, demultiplexer_1_out31;
  wire [31:0] registrador_1_out_3, registrador_2_out_3, registrador_3_out_3, registrador_4_out_3,
       registrador_5_out_3, registrador_6_out_3, registrador_7_out_3, registrador_8_out_3,
       registrador_9_out_3, registrador_10_out_3, registrador_11_out_3, registrador_12_out_3,
       registrador_13_out_3, registrador_14_out_3, registrador_15_out_3, registrador_16_out_3,
       registrador_17_out_3, registrador_18_out_3, registrador_19_out_3, registrador_20_out_3,
       registrador_21_out_3, registrador_22_out_3, registrador_23_out_3, registrador_24_out_3,
       registrador_25_out_3, registrador_26_out_3, registrador_27_out_3, registrador_28_out_3,
       registrador_29_out_3, registrador_30_out_3, registrador_31_out_3, registrador_32_out_3;

  Demultiplexer #(.select(5), .enable("false")) demultiplexer_1 (
    .out0(demultiplexer_1_out0), .out1(demultiplexer_1_out1), .out2(demultiplexer_1_out2),
    .out3(demultiplexer_1_out3), .out4(demultiplexer_1_out4), .out5(demultiplexer_1_out5),
    .out6(demultiplexer_1_out6), .out7(demultiplexer_1_out7), .out8(demultiplexer_1_out8),
    .out9(demultiplexer_1_out9), .out10(demultiplexer_1_out10), .out11(demultiplexer_1_out11),
    .out12(demultiplexer_1_out12), .out13(demultiplexer_1_out13), .out14(demultiplexer_1_out14),
    .out15(demultiplexer_1_out15), .out16(demultiplexer_1_out16), .out17(demultiplexer_1_out17),
    .out18(demultiplexer_1_out18), .out19(demultiplexer_1_out19), .out20(demultiplexer_1_out20),
    .out21(demultiplexer_1_out21), .out22(demultiplexer_1_out22), .out23(demultiplexer_1_out23),
    .out24(demultiplexer_1_out24), .out25(demultiplexer_1_out25), .out26(demultiplexer_1_out26),
    .out27(demultiplexer_1_out27), .out28(demultiplexer_1_out28), .out29(demultiplexer_1_out29),
    .out30(demultiplexer_1_out30), .out31(demultiplexer_1_out31), .in(Clock), .sel(in_4));
  registrador registrador_1 (.in_1(in_2), .in_2(demultiplexer_1_out7), .out_3(registrador_1_out_3));
  registrador registrador_2 (.in_1(in_2), .in_2(demultiplexer_1_out15), .out_3(registrador_2_out_3));
  registrador registrador_3 (.in_1(in_2), .in_2(demultiplexer_1_out23), .out_3(registrador_3_out_3));
  registrador registrador_4 (.in_1(in_2), .in_2(demultiplexer_1_out31), .out_3(registrador_4_out_3));
  registrador registrador_5 (.in_1(in_2), .in_2(demultiplexer_1_out6), .out_3(registrador_5_out_3));
  registrador registrador_6 (.in_1(in_2), .in_2(demultiplexer_1_out14), .out_3(registrador_6_out_3));
  registrador registrador_7 (.in_1(in_2), .in_2(demultiplexer_1_out22), .out_3(registrador_7_out_3));
  registrador registrador_8 (.in_1(in_2), .in_2(demultiplexer_1_out30), .out_3(registrador_8_out_3));
  registrador registrador_9 (.in_1(in_2), .in_2(demultiplexer_1_out5), .out_3(registrador_9_out_3));
  registrador registrador_10 (.in_1(in_2), .in_2(demultiplexer_1_out13), .out_3(registrador_10_out_3));
  registrador registrador_11 (.in_1(in_2), .in_2(demultiplexer_1_out21), .out_3(registrador_11_out_3));
  registrador registrador_12 (.in_1(in_2), .in_2(demultiplexer_1_out29), .out_3(registrador_12_out_3));
  registrador registrador_13 (.in_1(in_2), .in_2(demultiplexer_1_out4), .out_3(registrador_13_out_3));
  registrador registrador_14 (.in_1(in_2), .in_2(demultiplexer_1_out12), .out_3(registrador_14_out_3));
  registrador registrador_15 (.in_1(in_2), .in_2(demultiplexer_1_out20), .out_3(registrador_15_out_3));
  registrador registrador_16 (.in_1(in_2), .in_2(demultiplexer_1_out28), .out_3(registrador_16_out_3));
  registrador registrador_17 (.in_1(in_2), .in_2(demultiplexer_1_out3), .out_3(registrador_17_out_3));
  registrador registrador_18 (.in_1(in_2), .in_2(demultiplexer_1_out11), .out_3(registrador_18_out_3));
  registrador registrador_19 (.in_1(in_2), .in_2(demultiplexer_1_out19), .out_3(registrador_19_out_3));
  registrador registrador_20 (.in_1(in_2), .in_2(demultiplexer_1_out27), .out_3(registrador_20_out_3));
  registrador registrador_21 (.in_1(in_2), .in_2(demultiplexer_1_out2), .out_3(registrador_21_out_3));
  registrador registrador_22 (.in_1(in_2), .in_2(demultiplexer_1_out10), .out_3(registrador_22_out_3));
  registrador registrador_23 (.in_1(in_2), .in_2(demultiplexer_1_out18), .out_3(registrador_23_out_3));
  registrador registrador_24 (.in_1(in_2), .in_2(demultiplexer_1_out26), .out_3(registrador_24_out_3));
  registrador registrador_25 (.in_1(in_2), .in_2(demultiplexer_1_out1), .out_3(registrador_25_out_3));
  registrador registrador_26 (.in_1(in_2), .in_2(demultiplexer_1_out9), .out_3(registrador_26_out_3));
  registrador registrador_27 (.in_1(in_2), .in_2(demultiplexer_1_out17), .out_3(registrador_27_out_3));
  registrador registrador_28 (.in_1(in_2), .in_2(demultiplexer_1_out25), .out_3(registrador_28_out_3));
  registrador registrador_29 (.in_1({32{1'b0}}), .in_2(demultiplexer_1_out0), .out_3(registrador_29_out_3));
  registrador registrador_30 (.in_1(in_2), .in_2(demultiplexer_1_out8), .out_3(registrador_30_out_3));
  registrador registrador_31 (.in_1(in_2), .in_2(demultiplexer_1_out16), .out_3(registrador_31_out_3));
  registrador registrador_32 (.in_1(in_2), .in_2(demultiplexer_1_out24), .out_3(registrador_32_out_3));
  Multiplexer #(.select(5), .width(32), .enable("false")) multiplexer_1 (
    .in0(registrador_29_out_3), .in1(registrador_25_out_3), .in2(registrador_21_out_3),
    .in3(registrador_17_out_3), .in4(registrador_13_out_3), .in5(registrador_9_out_3),
    .in6(registrador_5_out_3), .in7(registrador_1_out_3), .in8(registrador_30_out_3),
    .in9(registrador_26_out_3), .in10(registrador_22_out_3), .in11(registrador_18_out_3),
    .in12(registrador_14_out_3), .in13(registrador_10_out_3), .in14(registrador_6_out_3),
    .in15(registrador_2_out_3), .in16(registrador_31_out_3), .in17(registrador_27_out_3),
    .in18(registrador_23_out_3), .in19(registrador_19_out_3), .in20(registrador_15_out_3),
    .in21(registrador_11_out_3), .in22(registrador_7_out_3), .in23(registrador_3_out_3),
    .in24(registrador_32_out_3), .in25(registrador_28_out_3), .in26(registrador_24_out_3),
    .in27(registrador_20_out_3), .in28(registrador_16_out_3), .in29(registrador_12_out_3),
    .in30(registrador_8_out_3), .in31(registrador_4_out_3), .out(out_7), .sel(in_5));
  Multiplexer #(.select(5), .width(32), .enable("false")) multiplexer_2 (
    .in0(registrador_29_out_3), .in1(registrador_25_out_3), .in2(registrador_21_out_3),
    .in3(registrador_17_out_3), .in4(registrador_13_out_3), .in5(registrador_9_out_3),
    .in6(registrador_5_out_3), .in7(registrador_1_out_3), .in8(registrador_30_out_3),
    .in9(registrador_26_out_3), .in10(registrador_22_out_3), .in11(registrador_18_out_3),
    .in12(registrador_14_out_3), .in13(registrador_10_out_3), .in14(registrador_6_out_3),
    .in15(registrador_2_out_3), .in16(registrador_31_out_3), .in17(registrador_27_out_3),
    .in18(registrador_23_out_3), .in19(registrador_19_out_3), .in20(registrador_15_out_3),
    .in21(registrador_11_out_3), .in22(registrador_7_out_3), .in23(registrador_3_out_3),
    .in24(registrador_32_out_3), .in25(registrador_28_out_3), .in26(registrador_24_out_3),
    .in27(registrador_20_out_3), .in28(registrador_16_out_3), .in29(registrador_12_out_3),
    .in30(registrador_8_out_3), .in31(registrador_4_out_3), .out(out_6), .sel(Oper_A));

  // Notes on the sheet:
  //   Oper Demux
  //   Entrada
  //   REG ZERO
  //   Saida A
  //   Saida B
  //   Oper B
endmodule

module processador (
  input  in_1,
  input  [31:0] in_2,
  input  I,
  input  [4:0] in_4,
  input  [19:0] in_5,
  input  in_6,
  output [31:0] out_7,
  output out_8,
  output out_9,
  output [7:0] Seletor
);

  wire [19:0] register_1_q;
  wire [31:0] banco_de_registradores_2_1_out_6, banco_de_registradores_2_1_out_7, multiplexer_1_out;

  PC pc_1 (.Clock(in_1), .Reset(in_6), .out_3(Seletor));
  Register #(.width(20)) register_1 (.D(in_5), .Q(register_1_q), .clk(in_1), .clr(in_6));  // open: en
  banco_de_registradores_2 banco_de_registradores_2_1 (
    .in_2(out_7), .Clock(in_1), .out_6(banco_de_registradores_2_1_out_6),
    .out_7(banco_de_registradores_2_1_out_7), .in_4(register_1_q[19:15]), .in_5(register_1_q[14:10]),
    .Oper_A(register_1_q[9:5]));
  RAM #(.dataWidth(20)) ram_1 ();  // open: addr, data, sel, clk, ld, clr
  Multiplexer #(.width(32), .enable("false")) multiplexer_1 (
    .in0(banco_de_registradores_2_1_out_6), .in1(in_2), .out(multiplexer_1_out), .sel(I));
  ula ula_1 (
    .in_1(in_4), .in_4(register_1_q[4:0]), .out_7(out_9), .in_2(multiplexer_1_out),
    .in_3(banco_de_registradores_2_1_out_7), .out_5(out_7), .Saida_0(out_8));

  // Notes on the sheet:
  //   Dados
  //   LEMBRAR DO REG ZERO
  //   00000 - AND
  //   00001 - OR
  //   00010 - NAND
  //   00011 - XOR  
  //    00100 - SOM N
  //    00101 - SOM Z
  //   00110 - SUB N
  //   00111 - SLT
  //   01000 - SLL
  //   01001 - SRL
  //   01010 - SRA
endmodule

module PC (
  input  Clock,
  input  Reset,
  output [7:0] out_3
);

  wire [7:0] adder_1_out;

  Adder adder_1 (.a(8'h1), .b(out_3), .out(adder_1_out));  // open: cin, cout
  Register register_1 (.D(adder_1_out), .Q(out_3), .clk(Clock), .clr(Reset));  // open: en

  // Notes on the sheet:
  //   Saida
endmodule
